// Logisim project 4bit_optimized.circ as structural Verilog
module RAM_1_Nibble (
  input  D0,
  input  CLK,
  input  D1,
  input  D2,
  input  D3,
  output O0,
  output O1,
  output O2,
  output O3
);

  D_Flip_Flop d_ff_1 (.D(D0), .clk(CLK), .Q(O0));  // open: Qn, preset, reset
  D_Flip_Flop d_ff_2 (.D(D1), .clk(CLK), .Q(O1));  // open: Qn, preset, reset
  D_Flip_Flop d_ff_3 (.D(D2), .clk(CLK), .Q(O2));  // open: Qn, preset, reset
  D_Flip_Flop d_ff_4 (.D(D3), .clk(CLK), .Q(O3));  // open: Qn, preset, reset
endmodule

module ram256x4 (
  input  [7:0] A,
  input  GO,
  input  [3:0] D,
  output [3:0] O
);

  RAM #(.dataWidth(4)) ram_1 (.addr(A), .we(GO), .oe(GO), .clk(GO), .din(D), .dout(O));
endmodule

module RAM_4_Nibble (
  input  A0,
  input  A1,
  input  CLK,
  input  D0,
  input  D1,
  input  D2,
  input  D3,
  output O0,
  output O1,
  output O2,
  output O3
);

  wire and_1_out, and_2_out, and_3_out, and_4_out, and_5_out, and_6_out, and_7_out, and_8_out, and_9_out,
       and_10_out, and_11_out, and_12_out, and_13_out, and_14_out, and_15_out, and_16_out, and_17_out,
       and_18_out, and_19_out, and_20_out, DATA_00_o0, DATA_00_o1, DATA_00_o2, DATA_00_o3, DATA_01_o0,
       DATA_01_o1, DATA_01_o2, DATA_01_o3, DATA_10_o0, DATA_10_o1, DATA_10_o2, DATA_10_o3, DATA_11_o0,
       DATA_11_o1, DATA_11_o2, DATA_11_o3, not_1_out, not_2_out, SCENARIO_00_out, SCENARIO_01_out,
       SCENARIO_10_out, SCENARIO_11_out;

  not not_1 (not_1_out, A0);
  not not_2 (not_2_out, A1);
  and SCENARIO_11 (SCENARIO_11_out, A0, A1);
  and SCENARIO_10 (SCENARIO_10_out, A0, not_2_out);
  and SCENARIO_01 (SCENARIO_01_out, not_1_out, A1);
  and SCENARIO_00 (SCENARIO_00_out, not_1_out, not_2_out);
  and and_1 (and_1_out, SCENARIO_11_out, CLK);
  and and_2 (and_2_out, SCENARIO_10_out, CLK);
  and and_3 (and_3_out, SCENARIO_01_out, CLK);
  and and_4 (and_4_out, SCENARIO_00_out, CLK);
  and and_5 (and_5_out, DATA_11_o0, SCENARIO_11_out);
  and and_6 (and_6_out, DATA_11_o1, SCENARIO_11_out);
  RAM_1_Nibble DATA_11 (
    .D0(D0), .CLK(and_1_out), .D1(D1), .D2(D2), .D3(D3), .O0(DATA_11_o0), .O1(DATA_11_o1), .O2(DATA_11_o2),
    .O3(DATA_11_o3));
  and and_7 (and_7_out, DATA_11_o2, SCENARIO_11_out);
  and and_8 (and_8_out, DATA_11_o3, SCENARIO_11_out);
  and and_9 (and_9_out, DATA_10_o0, SCENARIO_10_out);
  and and_10 (and_10_out, DATA_10_o1, SCENARIO_10_out);
  RAM_1_Nibble DATA_10 (
    .D0(D0), .CLK(and_2_out), .D1(D1), .D2(D2), .D3(D3), .O0(DATA_10_o0), .O1(DATA_10_o1), .O2(DATA_10_o2),
    .O3(DATA_10_o3));
  and and_11 (and_11_out, DATA_10_o2, SCENARIO_10_out);
  and and_12 (and_12_out, DATA_10_o3, SCENARIO_10_out);
  and and_13 (and_13_out, DATA_01_o0, SCENARIO_01_out);
  and and_14 (and_14_out, DATA_01_o1, SCENARIO_01_out);
  RAM_1_Nibble DATA_01 (
    .D0(D0), .CLK(and_3_out), .D1(D1), .D2(D2), .D3(D3), .O0(DATA_01_o0), .O1(DATA_01_o1), .O2(DATA_01_o2),
    .O3(DATA_01_o3));
  and and_15 (and_15_out, DATA_01_o2, SCENARIO_01_out);
  and and_16 (and_16_out, DATA_01_o3, SCENARIO_01_out);
  and and_17 (and_17_out, DATA_00_o0, SCENARIO_00_out);
  and and_18 (and_18_out, DATA_00_o1, SCENARIO_00_out);
  RAM_1_Nibble DATA_00 (
    .D0(D0), .CLK(and_4_out), .D1(D1), .D2(D2), .D3(D3), .O0(DATA_00_o0), .O1(DATA_00_o1), .O2(DATA_00_o2),
    .O3(DATA_00_o3));
  and and_19 (and_19_out, DATA_00_o2, SCENARIO_00_out);
  and and_20 (and_20_out, DATA_00_o3, SCENARIO_00_out);
  or O2_ACCUMULATOR (O2, and_11_out, and_7_out, and_15_out, and_19_out);
  or O3_ACCUMULATOR (O3, and_8_out, and_12_out, and_16_out, and_20_out);
  or O0_ACCUMULATOR (O0, and_5_out, and_9_out, and_13_out, and_17_out);
  or O1_ACCUMULATOR (O1, and_6_out, and_10_out, and_14_out, and_18_out);
endmodule

module RAM_16_Nibble (
  input  D0,
  input  D1,
  input  D2,
  input  D3,
  input  A0,
  input  A1,
  input  CLK,
  input  A2,
  input  A3,
  output O0,
  output O1,
  output O2,
  output O3
);

  wire and_1_out, and_2_out, and_3_out, and_4_out, and_5_out, and_6_out, and_7_out, and_8_out, and_9_out,
       and_10_out, and_11_out, and_12_out, and_13_out, and_14_out, and_15_out, and_16_out, and_17_out,
       and_18_out, and_19_out, and_20_out, DATA_00_o0, DATA_00_o1, DATA_00_o2, DATA_00_o3, DATA_01_o0,
       DATA_01_o1, DATA_01_o2, DATA_01_o3, DATA_10_o0, DATA_10_o1, DATA_10_o2, DATA_10_o3, DATA_11_o0,
       DATA_11_o1, DATA_11_o2, DATA_11_o3, not_1_out, not_2_out, SCENARIO_00_out, SCENARIO_01_out,
       SCENARIO_10_out, SCENARIO_11_out;

  not not_1 (not_1_out, A2);
  not not_2 (not_2_out, A3);
  and SCENARIO_11 (SCENARIO_11_out, A2, A3);
  and SCENARIO_10 (SCENARIO_10_out, A2, not_2_out);
  and SCENARIO_01 (SCENARIO_01_out, not_1_out, A3);
  and SCENARIO_00 (SCENARIO_00_out, not_1_out, not_2_out);
  and and_1 (and_1_out, CLK, SCENARIO_11_out);
  and and_2 (and_2_out, CLK, SCENARIO_10_out);
  and and_3 (and_3_out, CLK, SCENARIO_01_out);
  and and_4 (and_4_out, CLK, SCENARIO_00_out);
  RAM_4_Nibble DATA_11 (
    .A0(A0), .A1(A1), .CLK(and_1_out), .D0(D0), .D1(D1), .D2(D2), .D3(D3), .O0(DATA_11_o0), .O1(DATA_11_o1),
    .O2(DATA_11_o2), .O3(DATA_11_o3));
  RAM_4_Nibble DATA_10 (
    .A0(A0), .A1(A1), .CLK(and_2_out), .D0(D0), .D1(D1), .D2(D2), .D3(D3), .O0(DATA_10_o0), .O1(DATA_10_o1),
    .O2(DATA_10_o2), .O3(DATA_10_o3));
  RAM_4_Nibble DATA_01 (
    .A0(A0), .A1(A1), .CLK(and_3_out), .D0(D0), .D1(D1), .D2(D2), .D3(D3), .O0(DATA_01_o0), .O1(DATA_01_o1),
    .O2(DATA_01_o2), .O3(DATA_01_o3));
  RAM_4_Nibble DATA_00 (
    .A0(A0), .A1(A1), .CLK(and_4_out), .D0(D0), .D1(D1), .D2(D2), .D3(D3), .O0(DATA_00_o0), .O1(DATA_00_o1),
    .O2(DATA_00_o2), .O3(DATA_00_o3));
  and and_5 (and_5_out, DATA_11_o0, SCENARIO_11_out);
  and and_6 (and_6_out, DATA_11_o1, SCENARIO_11_out);
  and and_7 (and_7_out, DATA_11_o2, SCENARIO_11_out);
  and and_8 (and_8_out, DATA_11_o3, SCENARIO_11_out);
  and and_9 (and_9_out, DATA_10_o0, SCENARIO_10_out);
  and and_10 (and_10_out, DATA_10_o1, SCENARIO_10_out);
  and and_11 (and_11_out, DATA_10_o2, SCENARIO_10_out);
  and and_12 (and_12_out, DATA_10_o3, SCENARIO_10_out);
  and and_13 (and_13_out, DATA_01_o0, SCENARIO_01_out);
  and and_14 (and_14_out, DATA_01_o1, SCENARIO_01_out);
  and and_15 (and_15_out, DATA_01_o2, SCENARIO_01_out);
  and and_16 (and_16_out, DATA_01_o3, SCENARIO_01_out);
  and and_17 (and_17_out, DATA_00_o0, SCENARIO_00_out);
  and and_18 (and_18_out, DATA_00_o1, SCENARIO_00_out);
  and and_19 (and_19_out, DATA_00_o2, SCENARIO_00_out);
  and and_20 (and_20_out, DATA_00_o3, SCENARIO_00_out);
  or O0_ACCUMULATOR (O0, and_5_out, and_9_out, and_13_out, and_17_out);
  or O1_ACCUMULATOR (O1, and_6_out, and_10_out, and_14_out, and_18_out);
  or O2_ACCUMULATOR (O2, and_7_out, and_11_out, and_15_out, and_19_out);
  or O3_ACCUMULATOR (O3, and_8_out, and_12_out, and_16_out, and_20_out);
endmodule

module RAM_64_Nibble (
  input  D0,
  input  D1,
  input  D2,
  input  D3,
  input  A0,
  input  A1,
  input  A2,
  input  A3,
  input  CLK,
  input  A4,
  input  A5,
  output O0,
  output O1,
  output O2,
  output O3
);

  wire and_1_out, and_2_out, and_3_out, and_4_out, and_5_out, and_6_out, and_7_out, and_8_out, and_9_out,
       and_10_out, and_11_out, and_12_out, and_13_out, and_14_out, and_15_out, and_16_out, and_17_out,
       and_18_out, and_19_out, and_20_out, DATA_01_o0, DATA_01_o1, DATA_01_o2, DATA_01_o3, DATA_10_o0,
       DATA_10_o1, DATA_10_o2, DATA_10_o3, DATA_11_o0, DATA_11_o1, DATA_11_o2, DATA_11_o3, not_1_out,
       not_2_out, ram_16_nibble_1_o0, ram_16_nibble_1_o1, ram_16_nibble_1_o2, ram_16_nibble_1_o3,
       SCENARIO_00_out, SCENARIO_01_out, SCENARIO_10_out, SCENARIO_11_out;

  not not_1 (not_1_out, A4);
  not not_2 (not_2_out, A5);
  and SCENARIO_11 (SCENARIO_11_out, A4, A5);
  and SCENARIO_10 (SCENARIO_10_out, A4, not_2_out);
  and SCENARIO_01 (SCENARIO_01_out, not_1_out, A5);
  and SCENARIO_00 (SCENARIO_00_out, not_1_out, not_2_out);
  and and_1 (and_1_out, CLK, SCENARIO_11_out);
  and and_2 (and_2_out, CLK, SCENARIO_10_out);
  and and_3 (and_3_out, CLK, SCENARIO_01_out);
  and and_4 (and_4_out, CLK, SCENARIO_00_out);
  RAM_16_Nibble DATA_11 (
    .D0(D0), .D1(D1), .D2(D2), .D3(D3), .A0(A0), .A1(A1), .CLK(and_1_out), .A2(A2), .A3(A3), .O0(DATA_11_o0),
    .O1(DATA_11_o1), .O2(DATA_11_o2), .O3(DATA_11_o3));
  RAM_16_Nibble DATA_10 (
    .D0(D0), .D1(D1), .D2(D2), .D3(D3), .A0(A0), .A1(A1), .CLK(and_2_out), .A2(A2), .A3(A3), .O0(DATA_10_o0),
    .O1(DATA_10_o1), .O2(DATA_10_o2), .O3(DATA_10_o3));
  and and_5 (and_5_out, DATA_11_o0, CLK);
  and and_6 (and_6_out, DATA_11_o1, CLK);
  and and_7 (and_7_out, DATA_11_o2, CLK);
  and and_8 (and_8_out, DATA_11_o3, CLK);
  and and_9 (and_9_out, DATA_10_o0, SCENARIO_10_out);
  and and_10 (and_10_out, DATA_10_o1, SCENARIO_10_out);
  and and_11 (and_11_out, DATA_10_o2, SCENARIO_10_out);
  and and_12 (and_12_out, DATA_10_o3, SCENARIO_10_out);
  and and_13 (and_13_out, DATA_01_o0, SCENARIO_01_out);
  and and_14 (and_14_out, DATA_01_o1, SCENARIO_01_out);
  RAM_16_Nibble DATA_01 (
    .D0(D0), .D1(D1), .D2(D2), .D3(D3), .A0(A0), .A1(A1), .CLK(and_3_out), .A2(A2), .A3(A3), .O0(DATA_01_o0),
    .O1(DATA_01_o1), .O2(DATA_01_o2), .O3(DATA_01_o3));
  and and_15 (and_15_out, DATA_01_o2, SCENARIO_01_out);
  and and_16 (and_16_out, DATA_01_o3, SCENARIO_01_out);
  and and_17 (and_17_out, ram_16_nibble_1_o0, SCENARIO_00_out);
  and and_18 (and_18_out, ram_16_nibble_1_o1, SCENARIO_00_out);
  RAM_16_Nibble ram_16_nibble_1 (
    .D0(D0), .D1(D1), .D2(D2), .D3(D3), .A0(A0), .A1(A1), .CLK(and_4_out), .A2(A2), .A3(A3),
    .O0(ram_16_nibble_1_o0), .O1(ram_16_nibble_1_o1), .O2(ram_16_nibble_1_o2), .O3(ram_16_nibble_1_o3));
  and and_19 (and_19_out, ram_16_nibble_1_o2, SCENARIO_00_out);
  and and_20 (and_20_out, ram_16_nibble_1_o3, SCENARIO_00_out);
  or O0_ACCUMULATOR (O0, and_5_out, and_9_out, and_13_out, and_17_out);
  or O1_ACCUMULATOR (O1, and_6_out, and_10_out, and_14_out, and_18_out);
  or O2_ACCUMULATOR (O2, and_7_out, and_11_out, and_15_out, and_19_out);
  or O3_ACCUMULATOR (O3, and_8_out, and_12_out, and_16_out, and_20_out);
endmodule

module RAM_256_Nibble (
  input  D0,
  input  D1,
  input  D2,
  input  D3,
  input  A0,
  input  A1,
  input  A2,
  input  A3,
  input  A4,
  input  A5,
  input  CLK,
  input  A6,
  input  A7,
  output O0,
  output O1,
  output O2,
  output O3
);

  wire and_1_out, and_2_out, and_3_out, and_4_out, and_5_out, and_6_out, and_7_out, and_8_out, and_9_out,
       and_10_out, and_11_out, and_12_out, and_13_out, and_14_out, and_15_out, and_16_out, and_17_out,
       and_18_out, and_19_out, and_20_out, DATA_00_o0, DATA_00_o1, DATA_00_o2, DATA_00_o3, DATA_01_o0,
       DATA_01_o1, DATA_01_o2, DATA_01_o3, DATA_10_o0, DATA_10_o1, DATA_10_o2, DATA_10_o3, DATA_11_o0,
       DATA_11_o1, DATA_11_o2, DATA_11_o3, not_1_out, not_2_out, SCENARIO_00_out, SCENARIO_01_out,
       SCENARIO_10_out, SCENARIO_11_out;

  not not_1 (not_1_out, A6);
  not not_2 (not_2_out, A7);
  and SCENARIO_11 (SCENARIO_11_out, A6, A7);
  and SCENARIO_10 (SCENARIO_10_out, A6, not_2_out);
  and SCENARIO_01 (SCENARIO_01_out, not_1_out, A7);
  and SCENARIO_00 (SCENARIO_00_out, not_1_out, not_2_out);
  and and_1 (and_1_out, CLK, SCENARIO_11_out);
  and and_2 (and_2_out, CLK, SCENARIO_10_out);
  and and_3 (and_3_out, CLK, SCENARIO_01_out);
  and and_4 (and_4_out, CLK, SCENARIO_00_out);
  and and_5 (and_5_out, DATA_11_o0, SCENARIO_11_out);
  and and_6 (and_6_out, DATA_11_o1, SCENARIO_11_out);
  RAM_64_Nibble DATA_11 (
    .D0(D0), .D1(D1), .D2(D2), .D3(D3), .A0(A0), .A1(A1), .A2(A2), .A3(A3), .CLK(and_1_out), .A4(A4),
    .A5(A5), .O0(DATA_11_o0), .O1(DATA_11_o1), .O2(DATA_11_o2), .O3(DATA_11_o3));
  and and_7 (and_7_out, DATA_11_o2, SCENARIO_11_out);
  and and_8 (and_8_out, DATA_11_o3, SCENARIO_11_out);
  and and_9 (and_9_out, DATA_10_o0, SCENARIO_10_out);
  and and_10 (and_10_out, DATA_10_o1, SCENARIO_10_out);
  RAM_64_Nibble DATA_10 (
    .D0(D0), .D1(D1), .D2(D2), .D3(D3), .A0(A0), .A1(A1), .A2(A2), .A3(A3), .CLK(and_2_out), .A4(A4),
    .A5(A5), .O0(DATA_10_o0), .O1(DATA_10_o1), .O2(DATA_10_o2), .O3(DATA_10_o3));
  and and_11 (and_11_out, DATA_10_o2, SCENARIO_10_out);
  and and_12 (and_12_out, DATA_10_o3, SCENARIO_10_out);
  and and_13 (and_13_out, DATA_01_o0, SCENARIO_01_out);
  and and_14 (and_14_out, DATA_01_o1, SCENARIO_01_out);
  RAM_64_Nibble DATA_01 (
    .D0(D0), .D1(D1), .D2(D2), .D3(D3), .A0(A0), .A1(A1), .A2(A2), .A3(A3), .CLK(and_3_out), .A4(A4),
    .A5(A5), .O0(DATA_01_o0), .O1(DATA_01_o1), .O2(DATA_01_o2), .O3(DATA_01_o3));
  and and_15 (and_15_out, DATA_01_o2, SCENARIO_01_out);
  and and_16 (and_16_out, DATA_01_o3, SCENARIO_01_out);
  and and_17 (and_17_out, DATA_00_o0, SCENARIO_00_out);
  and and_18 (and_18_out, DATA_00_o1, SCENARIO_00_out);
  RAM_64_Nibble DATA_00 (
    .D0(D0), .D1(D1), .D2(D2), .D3(D3), .A0(A0), .A1(A1), .A2(A2), .A3(A3), .CLK(and_4_out), .A4(A4),
    .A5(A5), .O0(DATA_00_o0), .O1(DATA_00_o1), .O2(DATA_00_o2), .O3(DATA_00_o3));
  and and_19 (and_19_out, DATA_00_o2, SCENARIO_00_out);
  and and_20 (and_20_out, DATA_00_o3, SCENARIO_00_out);
  or O0_ACCUMULATOR (O0, and_5_out, and_9_out, and_13_out, and_17_out);
  or O1_ACCUMULATOR (O1, and_6_out, and_10_out, and_14_out, and_18_out);
  or O3_ACCUMULATOR (O3, and_8_out, and_12_out, and_16_out, and_20_out);
  or O2_ACCUMULATOR (O2, and_7_out, and_11_out, and_15_out, and_19_out);
endmodule

module ALU (
  input  OP0,
  input  OP1,
  input  OP2,
  input  D0,
  input  E0,
  input  D1,
  input  E1,
  input  D2,
  input  E2,
  input  D3,
  input  E3,
  output O0,
  output O1,
  output O2,
  output O3,
  output ERROR_BIT
);

  wire and_1_out, and_2_out, and_3_out, and_4_out, and_5_out, and_6_out, and_7_out, and_8_out, and_9_out,
       arithmetic_1_error_bit, arithmetic_1_out0, arithmetic_1_out1, arithmetic_1_out2, arithmetic_1_out3,
       logic_4_bit_1_o0, logic_4_bit_1_o1, logic_4_bit_1_o2, logic_4_bit_1_o3, not_1_out, not_2_out;

  not not_1 (not_1_out, OP0);
  and and_1 (and_1_out, not_1_out, OP2);
  and and_2 (and_2_out, logic_4_bit_1_o0, OP0);
  and and_3 (and_3_out, logic_4_bit_1_o1, OP0);
  LOGIC_4_BIT logic_4_bit_1 (
    .OP0(OP0), .OP1(OP1), .OP2(OP2), .D0(D0), .E0(E0), .D1(D1), .E1(E1), .D2(D2), .E2(E2), .D3(D3), .E3(E3),
    .O0(logic_4_bit_1_o0), .O1(logic_4_bit_1_o1), .O2(logic_4_bit_1_o2), .O3(logic_4_bit_1_o3));
  and and_4 (and_4_out, logic_4_bit_1_o2, OP0);
  and and_5 (and_5_out, logic_4_bit_1_o3, OP0);
  and and_6 (and_6_out, arithmetic_1_out3, not_2_out);
  and and_7 (and_7_out, arithmetic_1_out2, not_2_out);
  ARITHMETIC arithmetic_1 (
    .D3(D3), .E3(E3), .D2(D2), .E2(E2), .D1(D1), .E1(E1), .D0(D0), .E0(E0), .SUBTRACTION_BIT(and_1_out),
    .OUT3(arithmetic_1_out3), .OUT2(arithmetic_1_out2), .OUT1(arithmetic_1_out1), .OUT0(arithmetic_1_out0),
    .ERROR_BIT(arithmetic_1_error_bit));
  and and_8 (and_8_out, arithmetic_1_out1, not_2_out);
  and and_9 (and_9_out, arithmetic_1_out0, not_2_out);
  and and_10 (ERROR_BIT, arithmetic_1_error_bit, not_2_out);
  not not_2 (not_2_out, OP0);
  or O0_ACCUMULATOR (O0, and_2_out, and_9_out);
  or O1_ACCUMULATOR (O1, and_3_out, and_8_out);
  or O2_ACCUMULATOR (O2, and_4_out, and_7_out);
  or O3_ACCUMULATOR (O3, and_5_out, and_6_out);

  // Notes on the sheet:
  //   ALU - 0 is the highest bit
  //   000 - ADD
  //   001 - SUB
  //   010 - NOP
  //   011 - NOP
  //   100 - NOT
  //   101 - XOR
  //   110 - OR
  //   111 - AND
  //   (only on D3)
endmodule

module LOGIC (
  input  OP0,
  input  OP1,
  input  OP2,
  input  D0,
  input  E0,
  output O
);

  wire and_1_out, and_2_out, and_3_out, and_4_out, and_5_out, and_6_out, and_7_out, and_8_out, and_9_out,
       n7408_1_pin3, n7408_1_pin6, n7408_1_pin8, n7408_1_pin11, not_1_out, not_2_out, not_3_out, or_1_out,
       xor_1_out;

  not not_1 (not_1_out, OP1);
  not not_2 (not_2_out, OP2);
  and and_1 (and_1_out, OP1, OP2);
  and and_2 (and_2_out, OP1, not_2_out);
  and and_3 (and_3_out, not_1_out, OP2);
  and and_4 (and_4_out, not_1_out, not_2_out);
  and and_5 (and_5_out, OP0, and_1_out);
  and and_6 (and_6_out, OP0, and_2_out);
  and and_7 (and_7_out, OP0, and_3_out);
  and and_8 (and_8_out, OP0, and_4_out);
  and and_9 (and_9_out, D0, E0);
  or or_1 (or_1_out, D0, E0);
  xor xor_1 (xor_1_out, D0, E0);
  not not_3 (not_3_out, D0);
  _7408 u_7408_1 (
    .pin1(and_7_out), .pin2(xor_1_out), .pin3(n7408_1_pin3), .pin4(and_8_out), .pin5(not_3_out),
    .pin6(n7408_1_pin6), .pin13(and_5_out), .pin12(and_9_out), .pin11(n7408_1_pin11), .pin10(or_1_out),
    .pin9(and_6_out), .pin8(n7408_1_pin8));
  or or_2 (O, n7408_1_pin11, n7408_1_pin8, n7408_1_pin3, n7408_1_pin6);

  // Notes on the sheet:
  //   100 - NOT
  //   101 - XOR
  //   110 - OR
  //   111 - AND
  //   All prefixed by 1 - designed to be interfaced with the arithmetic unit (prefixed by 0)
  //   Logic Unit
  //   Takes data on D0 and E0
  //   (only on D0)
endmodule

module ARITHMETIC (
  input  D3,
  input  E3,
  input  D2,
  input  E2,
  input  D1,
  input  E1,
  input  D0,
  input  E0,
  input  SUBTRACTION_BIT,
  output OUT3,
  output OUT2,
  output OUT1,
  output OUT0,
  output ERROR_BIT
);

  wire adder_4_bit_carry_1_carry_out, adder_4_bit_carry_1_o0, adder_4_bit_carry_1_o1, adder_4_bit_carry_1_o2,
       adder_4_bit_carry_1_o3, and_1_out, and_2_out, and_3_out, and_4_out, and_5_out, and_6_out, and_7_out,
       and_8_out, and_9_out, and_10_out, not_1_out, subtracter_4_bit_overflow_1_diff0,
       subtracter_4_bit_overflow_1_diff1, subtracter_4_bit_overflow_1_diff2,
       subtracter_4_bit_overflow_1_diff3, subtracter_4_bit_overflow_1_overflow;

  and and_1 (and_1_out, adder_4_bit_carry_1_o0, not_1_out);
  and and_2 (and_2_out, adder_4_bit_carry_1_o1, not_1_out);
  Adder_4_Bit_Carry adder_4_bit_carry_1 (
    .d0(D3), .d1(E3), .d2(D2), .d3(E2), .e0(D1), .e1(E1), .carry_in(D0), .e2(E0),
    .o0(adder_4_bit_carry_1_o0), .o1(adder_4_bit_carry_1_o1), .o2(adder_4_bit_carry_1_o2),
    .o3(adder_4_bit_carry_1_o3), .carry_out(adder_4_bit_carry_1_carry_out));  // open: e3
  and and_3 (and_3_out, adder_4_bit_carry_1_o2, not_1_out);
  and and_4 (and_4_out, adder_4_bit_carry_1_o3, not_1_out);
  and and_5 (and_5_out, adder_4_bit_carry_1_carry_out, not_1_out);
  and and_6 (and_6_out, subtracter_4_bit_overflow_1_diff3, SUBTRACTION_BIT);
  and and_7 (and_7_out, subtracter_4_bit_overflow_1_diff2, SUBTRACTION_BIT);
  Subtracter_4_Bit_Overflow subtracter_4_bit_overflow_1 (
    .D3(D3), .E3(E3), .D2(D2), .E2(E2), .D1(D1), .E1(E1), .D0(D0), .E0(E0),
    .DIFF3(subtracter_4_bit_overflow_1_diff3), .DIFF2(subtracter_4_bit_overflow_1_diff2),
    .DIFF1(subtracter_4_bit_overflow_1_diff1), .DIFF0(subtracter_4_bit_overflow_1_diff0),
    .OVERFLOW(subtracter_4_bit_overflow_1_overflow));
  and and_8 (and_8_out, subtracter_4_bit_overflow_1_diff1, SUBTRACTION_BIT);
  and and_9 (and_9_out, subtracter_4_bit_overflow_1_diff0, SUBTRACTION_BIT);
  and and_10 (and_10_out, subtracter_4_bit_overflow_1_overflow, SUBTRACTION_BIT);
  not not_1 (not_1_out, SUBTRACTION_BIT);
  or or_1 (OUT3, and_1_out, and_6_out);
  or or_2 (OUT2, and_2_out, and_7_out);
  or or_3 (OUT1, and_3_out, and_8_out);
  or or_4 (OUT0, and_4_out, and_9_out);
  or or_5 (ERROR_BIT, and_5_out, and_10_out);
endmodule

module Adder_1_Bit_With_Carry (
  input  CARRY_IN,
  input  D0,
  input  D1,
  output SUM,
  output CARRY_OUT
);

  wire and_1_out, and_2_out, and_3_out, nand_1_out, nand_2_out, or_1_out, or_2_out;

  or or_1 (or_1_out, D0, D1);
  nand nand_1 (nand_1_out, D0, D1);
  and and_1 (and_1_out, D0, D1);
  and and_2 (and_2_out, or_1_out, nand_1_out);
  or or_2 (or_2_out, CARRY_IN, and_2_out);
  nand nand_2 (nand_2_out, CARRY_IN, and_2_out);
  and and_3 (and_3_out, CARRY_IN, and_2_out);
  and and_4 (SUM, or_2_out, nand_2_out);
  or or_3 (CARRY_OUT, and_3_out, and_1_out);
endmodule

module Adder_4_Bit_Carry (
  input  d0,
  input  d1,
  input  d2,
  input  d3,
  input  e0,
  input  e1,
  input  carry_in,
  input  e2,
  input  e3,
  output o0,
  output o1,
  output o2,
  output o3,
  output carry_out
);

  _74283 u_74283_1 (
    .pin1(o2), .pin2(d2), .pin3(e2), .pin4(o3), .pin5(d3), .pin6(e3), .pin7(carry_in), .pin15(e1),
    .pin14(d1), .pin13(o1), .pin12(e0), .pin11(d0), .pin10(o0), .pin9(carry_out));
endmodule

module Subtracter_4_Bit_Overflow (
  input  D3,
  input  E3,
  input  D2,
  input  E2,
  input  D1,
  input  E1,
  input  D0,
  input  E0,
  output DIFF3,
  output DIFF2,
  output DIFF1,
  output DIFF0,
  output OVERFLOW
);

  wire not_1_out, not_2_out, not_3_out, not_4_out, SUB_0_carry_out, SUB_1_carry_out, SUB_2_carry_out,
       SUB_3_carry_out;

  not not_1 (not_1_out, E3);
  not not_2 (not_2_out, E2);
  not not_3 (not_3_out, E1);
  not not_4 (not_4_out, E0);
  Adder_1_Bit_With_Carry SUB_3 (.CARRY_IN(1'b1), .D0(D3), .D1(not_1_out), .SUM(DIFF3), .CARRY_OUT(SUB_3_carry_out));
  Adder_1_Bit_With_Carry SUB_2 (
    .CARRY_IN(SUB_3_carry_out), .D0(D2), .D1(not_2_out), .SUM(DIFF2), .CARRY_OUT(SUB_2_carry_out));
  Adder_1_Bit_With_Carry SUB_1 (
    .CARRY_IN(SUB_2_carry_out), .D0(D1), .D1(not_3_out), .SUM(DIFF1), .CARRY_OUT(SUB_1_carry_out));
  Adder_1_Bit_With_Carry SUB_0 (
    .CARRY_IN(SUB_1_carry_out), .D0(D0), .D1(not_4_out), .SUM(DIFF0), .CARRY_OUT(SUB_0_carry_out));
  not not_5 (OVERFLOW, SUB_0_carry_out);

  // Notes on the sheet:
  //   0 is the highest bit
endmodule

module LOGIC_4_BIT (
  input  OP0,
  input  OP1,
  input  OP2,
  input  D0,
  input  E0,
  input  D1,
  input  E1,
  input  D2,
  input  E2,
  input  D3,
  input  E3,
  output O0,
  output O1,
  output O2,
  output O3
);

  wire n7400_1_pin3, n7400_1_pin6, n7400_1_pin8, n7400_1_pin11, n7408_1_pin1, n7408_1_pin2, n7408_1_pin3,
       n7408_1_pin6, n7408_1_pin8, n7408_1_pin11, n7408_2_pin3, n7408_2_pin6, n7408_2_pin8, n7408_2_pin11,
       n7408_3_pin2, n7408_3_pin3, n7408_3_pin6, n7408_3_pin8, n7408_3_pin11, n7408_4_pin3, n7408_4_pin6,
       n7408_4_pin8, n7408_5_pin3, n7408_5_pin6, n7408_5_pin8, n7408_5_pin11, n7408_6_pin3, n7408_6_pin6,
       n7408_6_pin8, n7408_6_pin11, n7432_1_pin3, n7432_1_pin6, n7432_1_pin8, n7432_1_pin11, n7486_1_pin3,
       n7486_1_pin6, n7486_1_pin8, n7486_1_pin11, QUAD_2_INPUT_AND_pin3, QUAD_2_INPUT_AND_pin6,
       QUAD_2_INPUT_AND_pin8, QUAD_2_INPUT_AND_pin11;

  _7408 u_7408_1 (
    .pin1(n7408_1_pin1), .pin2(n7408_1_pin2), .pin3(n7408_1_pin3), .pin4(n7408_1_pin2), .pin5(OP2),
    .pin6(n7408_1_pin6), .pin13(OP1), .pin12(n7408_1_pin1), .pin11(n7408_1_pin11), .pin10(OP2), .pin9(OP1),
    .pin8(n7408_1_pin8));
  not not_1 (n7408_1_pin2, OP1);
  not not_2 (n7408_1_pin1, OP2);
  _7408 u_7408_2 (
    .pin1(D0), .pin2(E0), .pin3(n7408_2_pin3), .pin4(D1), .pin5(E1), .pin6(n7408_2_pin6), .pin13(D2),
    .pin12(E2), .pin11(n7408_2_pin11), .pin10(D3), .pin9(E3), .pin8(n7408_2_pin8));
  _7408 u_7408_3 (
    .pin1(n7408_2_pin8), .pin2(n7408_3_pin2), .pin3(n7408_3_pin3), .pin4(n7408_2_pin11), .pin5(n7408_3_pin2),
    .pin6(n7408_3_pin6), .pin13(n7408_2_pin3), .pin12(n7408_3_pin2), .pin11(n7408_3_pin11),
    .pin10(n7408_2_pin6), .pin9(n7408_3_pin2), .pin8(n7408_3_pin8));
  _7408 u_7408_4 (
    .pin1(n7408_1_pin6), .pin2(OP0), .pin3(n7408_4_pin3), .pin4(n7408_1_pin3), .pin5(OP0),
    .pin6(n7408_4_pin6), .pin13(OP0), .pin12(n7408_1_pin8), .pin11(n7408_3_pin2), .pin10(OP0),
    .pin9(n7408_1_pin11), .pin8(n7408_4_pin8));
  _7432 u_7432_1 (
    .pin1(D0), .pin2(E0), .pin3(n7432_1_pin3), .pin4(D1), .pin5(E1), .pin6(n7432_1_pin6), .pin13(D2),
    .pin12(E2), .pin11(n7432_1_pin11), .pin10(D3), .pin9(E3), .pin8(n7432_1_pin8));
  _7408 u_7408_5 (
    .pin1(n7432_1_pin11), .pin2(n7408_4_pin8), .pin3(n7408_5_pin3), .pin4(n7432_1_pin8), .pin5(n7408_4_pin8),
    .pin6(n7408_5_pin6), .pin13(n7432_1_pin3), .pin12(n7408_4_pin8), .pin11(n7408_5_pin11),
    .pin10(n7432_1_pin6), .pin9(n7408_4_pin8), .pin8(n7408_5_pin8));
  _7486 u_7486_1 (
    .pin1(D0), .pin2(E0), .pin3(n7486_1_pin3), .pin4(D1), .pin5(E1), .pin6(n7486_1_pin6), .pin13(D2),
    .pin12(E2), .pin11(n7486_1_pin11), .pin10(D3), .pin9(E3), .pin8(n7486_1_pin8));
  _7400 u_7400_1 (
    .pin1(D3), .pin2(D3), .pin3(n7400_1_pin3), .pin4(D0), .pin5(D0), .pin6(n7400_1_pin6), .pin13(D2),
    .pin12(D2), .pin11(n7400_1_pin11), .pin10(D1), .pin9(D1), .pin8(n7400_1_pin8));
  _7408 u_7408_6 (
    .pin1(n7486_1_pin6), .pin2(n7408_4_pin3), .pin3(n7408_6_pin3), .pin4(n7486_1_pin3), .pin5(n7408_4_pin3),
    .pin6(n7408_6_pin6), .pin13(n7408_4_pin3), .pin12(n7486_1_pin8), .pin11(n7408_6_pin11),
    .pin10(n7408_4_pin3), .pin9(n7486_1_pin11), .pin8(n7408_6_pin8));
  _7408 QUAD_2_INPUT_AND (
    .pin1(n7400_1_pin8), .pin2(n7408_4_pin6), .pin3(QUAD_2_INPUT_AND_pin3), .pin4(n7400_1_pin11),
    .pin5(n7408_4_pin6), .pin6(QUAD_2_INPUT_AND_pin6), .pin13(n7400_1_pin6), .pin12(n7408_4_pin6),
    .pin11(QUAD_2_INPUT_AND_pin11), .pin10(n7408_4_pin6), .pin9(n7400_1_pin3), .pin8(QUAD_2_INPUT_AND_pin8));
  or O0_ACCUMULATOR (O0, QUAD_2_INPUT_AND_pin11, n7408_6_pin6, n7408_3_pin11, n7408_5_pin11);
  or O1_ACCUMULATOR (O1, QUAD_2_INPUT_AND_pin3, n7408_6_pin3, n7408_5_pin8, n7408_3_pin8);
  or O2_ACCUMULATOR (O2, QUAD_2_INPUT_AND_pin6, n7408_6_pin8, n7408_5_pin3, n7408_3_pin6);
  or O3_ACCUMULATOR (O3, QUAD_2_INPUT_AND_pin8, n7408_6_pin11, n7408_5_pin6, n7408_3_pin3);

  // Notes on the sheet:
  //   AND_CHECKERS
  //   OR_CHECKERS
  //   100 - NOT
  //   101 - XOR
  //   110 - OR
  //   111 - AND
  //   XOR CHECKERS
  //   (only on D0)
  //   NOT CHECKERS
  //   Replace these with 2 4072 ICs
  //   dual 4 input or
endmodule

module CONTROL (
  input  GO,
  input  OP0,
  input  OP1,
  input  OP2,
  input  OP3,
  input  A_ARG_0,
  input  A_ARG_1,
  input  A_ARG_2,
  input  A_ARG_3,
  input  A_ARG_4,
  input  A_ARG_5,
  input  A_ARG_6,
  input  A_ARG_7,
  input  B_ARG_0,
  input  B_ARG_1,
  input  B_ARD_2,
  input  B_ARG_3,
  input  B_ARG_4,
  input  B_ARG_5,
  input  B_ARG_6,
  input  B_ARG_7,
  output O0,
  output O1,
  output O2,
  output O3,
  output ERROR_BIT
);

  wire alu_1_error_bit, alu_1_o0, alu_1_o1, alu_1_o2, alu_1_o3, and_1_out, and_2_out, and_3_out, and_4_out,
       and_5_out, and_6_out, and_7_out, and_9_out, and_10_out, and_11_out, and_12_out, and_13_out,
       and_14_out, and_15_out, and_16_out, and_17_out, not_1_out, undriven, undriven_2, undriven_3,
       undriven_4;

  not not_1 (not_1_out, OP0);
  and and_1 (and_1_out, OP1, not_1_out);
  and and_2 (and_2_out, OP2, not_1_out);
  and and_3 (and_3_out, OP3, not_1_out);
  and and_4 (and_4_out, GO, and_9_out);
  and and_5 (and_5_out, GO, and_10_out);
  and and_6 (and_6_out, GO, and_11_out);
  and and_7 (and_7_out, GO, and_12_out);
  and and_8 (ERROR_BIT, GO, and_13_out);
  and and_9 (and_9_out, alu_1_o0, not_1_out);
  and and_10 (and_10_out, alu_1_o1, not_1_out);
  ALU alu_1 (
    .OP0(and_1_out), .OP1(and_2_out), .OP2(and_3_out), .D0(A_ARG_4), .E0(B_ARG_4), .D1(A_ARG_5),
    .E1(B_ARG_5), .D2(A_ARG_6), .E2(B_ARG_6), .D3(A_ARG_7), .E3(B_ARG_7), .O0(alu_1_o0), .O1(alu_1_o1),
    .O2(alu_1_o2), .O3(alu_1_o3), .ERROR_BIT(alu_1_error_bit));
  and and_11 (and_11_out, alu_1_o2, not_1_out);
  and and_12 (and_12_out, alu_1_o3, not_1_out);
  and and_13 (and_13_out, alu_1_error_bit, not_1_out);
  and and_14 (and_14_out, undriven, OP0);
  and and_15 (and_15_out, undriven_2, OP0);
  MEMORY memory_1 (
    .REG_D0(undriven), .REG_D1(undriven_2), .REG_D2(undriven_3), .REG_D3(undriven_4));  // open: OP0, OP1, OP2, OP3, WRITE_TO_REGISTER, A_ARG_0, A_ARG_1, A_ARG_2, A_ARG_3, A_ARG_4, A_ARG_5, A_ARG_6, A_ARG_7, B_ARG_0, B_ARG_1, B_ARD_2, B_ARG_3, B_ARG_4, B_ARG_5, B_ARG_6, B_ARG_7, GO
  and and_16 (and_16_out, undriven_3, OP0);
  and and_17 (and_17_out, undriven_4, OP0);
  or or_1 (O0, and_4_out, and_14_out);
  or or_2 (O1, and_5_out, and_15_out);
  or or_3 (O2, and_6_out, and_16_out);
  or or_4 (O3, and_7_out, and_17_out);
  LED led_1 (.in(O0));
  LED led_2 (.in(O1));
  LED led_3 (.in(O2));
  LED led_4 (.in(O3));
  LED led_5 (.in(ERROR_BIT));

  // Notes on the sheet:
  //   000 - ADD - LITERAL, LITERAL
  //   001 - SUB - LITERAL, LITERAL
  //   010 - NOP - IGNORED x2
  //   011 - NOP - IGNORED x2
  //   100 - NOT - LITERAL, IGNORED
  //   101 - XOR - LITERAL, LITERAL
  //   110 - OR - LITERAL, LITERAL
  //   111 - AND - LITERAL, LITERAL
  //   1000 - SAV - LITERAL, ADDR
  //   1001 - MOV - ADDR, ADDR
  //   This is the control unit - it takes in an opcode and two input sets
  //   OP0 through 3 are op codes - specified above
  //   The A_ARG and B_ARG sets are either a binary literal or a memory address
  //   This depends on the opcode, again specified above
  //   If they are literals, the top 4 bits must be 0 - the bottom 4 are the relevant ones
endmodule

module MEMORY (
  input  REG_D0,
  input  REG_D1,
  input  REG_D2,
  input  REG_D3,
  input  OP0,
  input  OP1,
  input  OP2,
  input  OP3,
  input  WRITE_TO_REGISTER,
  input  A_ARG_0,
  input  A_ARG_1,
  input  A_ARG_2,
  input  A_ARG_3,
  input  A_ARG_4,
  input  A_ARG_5,
  input  A_ARG_6,
  input  A_ARG_7,
  input  B_ARG_0,
  input  B_ARG_1,
  input  B_ARD_2,
  input  B_ARG_3,
  input  B_ARG_4,
  input  B_ARG_5,
  input  B_ARG_6,
  input  B_ARG_7,
  input  GO
);

  wire DATA_NEGATER_pin3, DATA_NEGATER_pin6, DATA_NEGATER_pin8, DATA_NEGATER_pin11, LDA_CHECKER_pin11,
       n7408_1_pin11, OP_INPUT_CHECKER_HI_BIT_pin6, OP_INPUT_CHECKER_LO_3_BITS_pin6,
       OP_INPUT_CHECKER_LO_3_BITS_pin12, OP_INPUT_NEGATER_pin3, OP_INPUT_NEGATER_pin8,
       OP_INPUT_NEGATER_pin11, OVERWRITE_CHECKER_ON_NEGATED_DATA_pin2,
       OVERWRITE_CHECKER_ON_NEGATED_DATA_pin3, OVERWRITE_CHECKER_ON_NEGATED_DATA_pin6,
       OVERWRITE_CHECKER_ON_NEGATED_DATA_pin8, OVERWRITE_CHECKER_ON_NEGATED_DATA_pin11,
       REGISTER_00_ACCUMULATOR_pin3, REGISTER_00_ACCUMULATOR_pin6, REGISTER_00_ACCUMULATOR_pin8,
       REGISTER_00_ACCUMULATOR_pin11, REGISTER_01_ACCUMULATOR_pin3, REGISTER_01_ACCUMULATOR_pin6,
       REGISTER_01_ACCUMULATOR_pin8, REGISTER_01_ACCUMULATOR_pin11, REGISTER_10_ACCUMULATOR_pin3,
       REGISTER_10_ACCUMULATOR_pin6, REGISTER_10_ACCUMULATOR_pin8, REGISTER_10_ACCUMULATOR_pin11,
       REGISTER_11_ACCUMULATOR_pin3, REGISTER_11_ACCUMULATOR_pin6, REGISTER_11_ACCUMULATOR_pin8,
       REGISTER_11_ACCUMULATOR_pin11, REGISTER_OUT_CHECKERS_pin1, REGISTER_OUT_CHECKERS_pin2,
       REGISTER_OUT_CHECKERS_pin3, REGISTER_OUT_CHECKERS_pin5, REGISTER_OUT_CHECKERS_pin6,
       REGISTER_OUT_CHECKERS_pin8, REGISTER_OUT_CHECKERS_pin10, REGISTER_OUT_CHECKERS_pin11,
       REGISTER_OUT_CHECKERS_pin12, REGISTER_SELECTOR_NEGATER_pin3, REGISTER_SELECTOR_NEGATER_pin6,
       REGISTER_SELECTOR_pin3, REGISTER_SELECTOR_pin6, REGISTER_SELECTOR_pin8, REGISTER_SELECTOR_pin11,
       REGISTER_WRITER_pin3, REGISTER_WRITER_pin6, REGISTER_WRITER_pin8, REGISTER_WRITER_pin11,
       SAV_LITERAL_CHECKER_pin1, SAV_LITERAL_CHECKER_pin3, SAV_LITERAL_CHECKER_pin6,
       SAV_LITERAL_CHECKER_pin8, SAV_LITERAL_CHECKER_pin11, WRITE_AND_OUTPUT_ACCUMULATORS_pin3,
       WRITE_AND_OUTPUT_ACCUMULATORS_pin6, WRITE_AND_OUTPUT_ACCUMULATORS_pin11;
  wire [3:0] DATA_IN_ACCUMULATOR_pin11, EXTERNAL_OR_INTERNAL_INPUT_ACCUMULATORS_pin6, ram_1_dout,
       register_1_q, register_2_q, register_3_q, register_4_q;

  _7408 SAV_LITERAL_CHECKER (
    .pin1(SAV_LITERAL_CHECKER_pin1), .pin2(B_ARG_5), .pin3(SAV_LITERAL_CHECKER_pin3),
    .pin4(SAV_LITERAL_CHECKER_pin1), .pin5(B_ARG_4), .pin6(SAV_LITERAL_CHECKER_pin6),
    .pin13(SAV_LITERAL_CHECKER_pin1), .pin12(B_ARG_7), .pin11(SAV_LITERAL_CHECKER_pin11),
    .pin10(SAV_LITERAL_CHECKER_pin1), .pin9(B_ARG_6), .pin8(SAV_LITERAL_CHECKER_pin8));
  _7400 OP_INPUT_NEGATER (
    .pin1(OP2), .pin2(OP2), .pin3(OP_INPUT_NEGATER_pin3), .pin13(OP1), .pin12(OP1),
    .pin11(OP_INPUT_NEGATER_pin11), .pin10(OP3), .pin9(OP3), .pin8(OP_INPUT_NEGATER_pin8));  // open: pin4, pin5, pin6
  _7411 OP_INPUT_CHECKER_LO_3_BITS (
    .pin1(OP_INPUT_NEGATER_pin11), .pin2(OP_INPUT_NEGATER_pin8), .pin3(OP3), .pin4(OP_INPUT_NEGATER_pin3),
    .pin5(OP_INPUT_NEGATER_pin11), .pin6(OP_INPUT_CHECKER_LO_3_BITS_pin6), .pin13(OP_INPUT_NEGATER_pin3),
    .pin12(OP_INPUT_CHECKER_LO_3_BITS_pin12));  // open: pin11, pin10, pin9, pin8
  _7408 REGISTER_OUT_CHECKERS (
    .pin1(REGISTER_OUT_CHECKERS_pin1), .pin2(REGISTER_OUT_CHECKERS_pin2), .pin3(REGISTER_OUT_CHECKERS_pin3),
    .pin4(REGISTER_OUT_CHECKERS_pin1), .pin5(REGISTER_OUT_CHECKERS_pin5), .pin6(REGISTER_OUT_CHECKERS_pin6),
    .pin13(REGISTER_OUT_CHECKERS_pin1), .pin12(REGISTER_OUT_CHECKERS_pin12),
    .pin11(REGISTER_OUT_CHECKERS_pin11), .pin10(REGISTER_OUT_CHECKERS_pin10),
    .pin9(REGISTER_OUT_CHECKERS_pin1), .pin8(REGISTER_OUT_CHECKERS_pin8));
  _7432 DATA_IN_ACCUMULATOR (
    .pin1(SAV_LITERAL_CHECKER_pin3), .pin2(REGISTER_OUT_CHECKERS_pin8), .pin3(DATA_IN_ACCUMULATOR_pin11[2]),
    .pin4(SAV_LITERAL_CHECKER_pin6), .pin5(REGISTER_OUT_CHECKERS_pin11), .pin6(DATA_IN_ACCUMULATOR_pin11[3]),
    .pin13(SAV_LITERAL_CHECKER_pin11), .pin12(REGISTER_OUT_CHECKERS_pin6),
    .pin11(DATA_IN_ACCUMULATOR_pin11[0]), .pin10(SAV_LITERAL_CHECKER_pin8),
    .pin9(REGISTER_OUT_CHECKERS_pin3), .pin8(DATA_IN_ACCUMULATOR_pin11[1]));
  _7408 OP_INPUT_CHECKER_HI_BIT (
    .pin1(OP_INPUT_CHECKER_LO_3_BITS_pin12), .pin2(OP0), .pin3(SAV_LITERAL_CHECKER_pin1),
    .pin4(OP_INPUT_CHECKER_LO_3_BITS_pin6), .pin5(OP0), .pin6(OP_INPUT_CHECKER_HI_BIT_pin6), .pin13(OP2),
    .pin12(OP_INPUT_NEGATER_pin8), .pin11(REGISTER_OUT_CHECKERS_pin1));  // open: pin10, pin9, pin8
  _7432 WRITE_AND_OUTPUT_ACCUMULATORS (
    .pin1(GO), .pin2(OP_INPUT_CHECKER_HI_BIT_pin6), .pin3(WRITE_AND_OUTPUT_ACCUMULATORS_pin3),
    .pin4(WRITE_AND_OUTPUT_ACCUMULATORS_pin3), .pin5(REGISTER_OUT_CHECKERS_pin1),
    .pin6(WRITE_AND_OUTPUT_ACCUMULATORS_pin6), .pin13(REGISTER_OUT_CHECKERS_pin1),
    .pin12(SAV_LITERAL_CHECKER_pin1), .pin11(WRITE_AND_OUTPUT_ACCUMULATORS_pin11));  // open: pin10, pin9, pin8
  RAM #(.dataWidth(4)) ram_1 (
    .addr({A_ARG_0, A_ARG_1, A_ARG_2, A_ARG_3, A_ARG_4, A_ARG_5, A_ARG_6, A_ARG_7}),
    .we(WRITE_AND_OUTPUT_ACCUMULATORS_pin11), .oe(WRITE_AND_OUTPUT_ACCUMULATORS_pin6), .clk(GO),
    .din(DATA_IN_ACCUMULATOR_pin11), .dout(ram_1_dout));
  _7400 REGISTER_SELECTOR_NEGATER (
    .pin1(B_ARG_6), .pin2(B_ARG_6), .pin3(REGISTER_SELECTOR_NEGATER_pin3), .pin4(B_ARG_7), .pin5(B_ARG_7),
    .pin6(REGISTER_SELECTOR_NEGATER_pin6));  // open: pin13, pin12, pin11, pin10, pin9, pin8
  _7408 REGISTER_SELECTOR (
    .pin1(B_ARG_6), .pin2(REGISTER_SELECTOR_NEGATER_pin6), .pin3(REGISTER_SELECTOR_pin3), .pin4(B_ARG_6),
    .pin5(B_ARG_7), .pin6(REGISTER_SELECTOR_pin6), .pin13(REGISTER_SELECTOR_NEGATER_pin3),
    .pin12(REGISTER_SELECTOR_NEGATER_pin6), .pin11(REGISTER_SELECTOR_pin11), .pin10(B_ARG_7),
    .pin9(REGISTER_SELECTOR_NEGATER_pin3), .pin8(REGISTER_SELECTOR_pin8));
  _7400 DATA_NEGATER (
    .pin1(ram_1_dout[2]), .pin2(ram_1_dout[2]), .pin3(DATA_NEGATER_pin3), .pin4(ram_1_dout[3]),
    .pin5(ram_1_dout[3]), .pin6(DATA_NEGATER_pin6), .pin13(ram_1_dout[0]), .pin12(ram_1_dout[0]),
    .pin11(DATA_NEGATER_pin11), .pin10(ram_1_dout[1]), .pin9(ram_1_dout[1]), .pin8(DATA_NEGATER_pin8));
  _7408 u_7408_1 (
    .pin13(OP_INPUT_CHECKER_HI_BIT_pin6), .pin12(GO), .pin11(n7408_1_pin11));  // open: pin1, pin2, pin3, pin4, pin5, pin6, pin10, pin9, pin8
  _7436 OVERWRITE_CHECKER_ON_NEGATED_DATA (
    .pin1(DATA_NEGATER_pin3), .pin2(OVERWRITE_CHECKER_ON_NEGATED_DATA_pin2),
    .pin3(OVERWRITE_CHECKER_ON_NEGATED_DATA_pin3), .pin4(DATA_NEGATER_pin6),
    .pin5(OVERWRITE_CHECKER_ON_NEGATED_DATA_pin2), .pin6(OVERWRITE_CHECKER_ON_NEGATED_DATA_pin6),
    .pin13(DATA_NEGATER_pin11), .pin12(OVERWRITE_CHECKER_ON_NEGATED_DATA_pin2),
    .pin11(OVERWRITE_CHECKER_ON_NEGATED_DATA_pin11), .pin10(DATA_NEGATER_pin8),
    .pin9(OVERWRITE_CHECKER_ON_NEGATED_DATA_pin2), .pin8(OVERWRITE_CHECKER_ON_NEGATED_DATA_pin8));
  _7408 REGISTER_WRITER (
    .pin1(REGISTER_SELECTOR_pin3), .pin2(WRITE_TO_REGISTER), .pin3(REGISTER_WRITER_pin3),
    .pin4(REGISTER_SELECTOR_pin6), .pin5(WRITE_TO_REGISTER), .pin6(REGISTER_WRITER_pin6),
    .pin13(REGISTER_SELECTOR_pin11), .pin12(WRITE_TO_REGISTER), .pin11(REGISTER_WRITER_pin11),
    .pin10(WRITE_TO_REGISTER), .pin9(REGISTER_SELECTOR_pin8), .pin8(REGISTER_WRITER_pin8));
  or or_1 (OVERWRITE_CHECKER_ON_NEGATED_DATA_pin2, REG_D0, REG_D1, REG_D2, REG_D3);
  _7432 LDA_CHECKER (
    .pin13(n7408_1_pin11), .pin12(REGISTER_WRITER_pin6), .pin11(LDA_CHECKER_pin11));  // open: pin1, pin2, pin3, pin4, pin5, pin6, pin10, pin9, pin8
  Register #(.width(4)) register_1 (
    .D(EXTERNAL_OR_INTERNAL_INPUT_ACCUMULATORS_pin6), .en(REGISTER_WRITER_pin11),
    .clk(REGISTER_WRITER_pin11), .Q(register_1_q));  // open: clr
  Register #(.width(4)) register_2 (
    .D(EXTERNAL_OR_INTERNAL_INPUT_ACCUMULATORS_pin6), .en(REGISTER_WRITER_pin8), .clk(REGISTER_WRITER_pin8),
    .Q(register_2_q));  // open: clr
  Register #(.width(4)) register_3 (
    .D(EXTERNAL_OR_INTERNAL_INPUT_ACCUMULATORS_pin6), .en(REGISTER_WRITER_pin3), .clk(REGISTER_WRITER_pin3),
    .Q(register_3_q));  // open: clr
  Register #(.width(4)) register_4 (
    .D(EXTERNAL_OR_INTERNAL_INPUT_ACCUMULATORS_pin6), .en(LDA_CHECKER_pin11), .clk(LDA_CHECKER_pin11),
    .Q(register_4_q));  // open: clr
  _7432 EXTERNAL_OR_INTERNAL_INPUT_ACCUMULATORS (
    .pin1(OVERWRITE_CHECKER_ON_NEGATED_DATA_pin8), .pin2(REG_D2),
    .pin3(EXTERNAL_OR_INTERNAL_INPUT_ACCUMULATORS_pin6[1]), .pin4(REG_D3),
    .pin5(OVERWRITE_CHECKER_ON_NEGATED_DATA_pin11), .pin6(EXTERNAL_OR_INTERNAL_INPUT_ACCUMULATORS_pin6[0]),
    .pin13(OVERWRITE_CHECKER_ON_NEGATED_DATA_pin6), .pin12(REG_D0),
    .pin11(EXTERNAL_OR_INTERNAL_INPUT_ACCUMULATORS_pin6[3]), .pin10(OVERWRITE_CHECKER_ON_NEGATED_DATA_pin3),
    .pin9(REG_D1), .pin8(EXTERNAL_OR_INTERNAL_INPUT_ACCUMULATORS_pin6[2]));
  _7408 REGISTER_00_ACCUMULATOR (
    .pin1(register_1_q[1]), .pin2(REGISTER_SELECTOR_pin11), .pin3(REGISTER_00_ACCUMULATOR_pin3),
    .pin4(register_1_q[0]), .pin5(REGISTER_SELECTOR_pin11), .pin6(REGISTER_00_ACCUMULATOR_pin6),
    .pin13(register_1_q[3]), .pin12(REGISTER_SELECTOR_pin11), .pin11(REGISTER_00_ACCUMULATOR_pin11),
    .pin10(register_1_q[2]), .pin9(REGISTER_SELECTOR_pin11), .pin8(REGISTER_00_ACCUMULATOR_pin8));
  _7408 REGISTER_01_ACCUMULATOR (
    .pin1(register_2_q[1]), .pin2(REGISTER_SELECTOR_pin8), .pin3(REGISTER_01_ACCUMULATOR_pin3),
    .pin4(register_2_q[0]), .pin5(REGISTER_SELECTOR_pin8), .pin6(REGISTER_01_ACCUMULATOR_pin6),
    .pin13(register_2_q[3]), .pin12(REGISTER_SELECTOR_pin8), .pin11(REGISTER_01_ACCUMULATOR_pin11),
    .pin10(register_2_q[2]), .pin9(REGISTER_SELECTOR_pin8), .pin8(REGISTER_01_ACCUMULATOR_pin8));
  _7408 REGISTER_10_ACCUMULATOR (
    .pin1(register_3_q[1]), .pin2(REGISTER_SELECTOR_pin3), .pin3(REGISTER_10_ACCUMULATOR_pin3),
    .pin4(register_3_q[0]), .pin5(REGISTER_SELECTOR_pin3), .pin6(REGISTER_10_ACCUMULATOR_pin6),
    .pin13(register_3_q[3]), .pin12(REGISTER_SELECTOR_pin3), .pin11(REGISTER_10_ACCUMULATOR_pin11),
    .pin10(register_3_q[2]), .pin9(REGISTER_SELECTOR_pin3), .pin8(REGISTER_10_ACCUMULATOR_pin8));
  _7408 REGISTER_11_ACCUMULATOR (
    .pin1(register_4_q[1]), .pin2(REGISTER_SELECTOR_pin6), .pin3(REGISTER_11_ACCUMULATOR_pin3),
    .pin4(register_4_q[0]), .pin5(REGISTER_SELECTOR_pin6), .pin6(REGISTER_11_ACCUMULATOR_pin6),
    .pin13(register_4_q[3]), .pin12(REGISTER_SELECTOR_pin6), .pin11(REGISTER_11_ACCUMULATOR_pin11),
    .pin10(register_4_q[2]), .pin9(REGISTER_SELECTOR_pin6), .pin8(REGISTER_11_ACCUMULATOR_pin8));
  or or_2 (REGISTER_OUT_CHECKERS_pin12, REGISTER_00_ACCUMULATOR_pin11, REGISTER_01_ACCUMULATOR_pin11, REGISTER_10_ACCUMULATOR_pin11, REGISTER_11_ACCUMULATOR_pin11);
  or or_3 (REGISTER_OUT_CHECKERS_pin10, REGISTER_00_ACCUMULATOR_pin8, REGISTER_01_ACCUMULATOR_pin8, REGISTER_10_ACCUMULATOR_pin8, REGISTER_11_ACCUMULATOR_pin8);
  or or_4 (REGISTER_OUT_CHECKERS_pin2, REGISTER_00_ACCUMULATOR_pin3, REGISTER_01_ACCUMULATOR_pin3, REGISTER_10_ACCUMULATOR_pin3, REGISTER_11_ACCUMULATOR_pin3);
  or or_5 (REGISTER_OUT_CHECKERS_pin5, REGISTER_00_ACCUMULATOR_pin6, REGISTER_01_ACCUMULATOR_pin6, REGISTER_10_ACCUMULATOR_pin6, REGISTER_11_ACCUMULATOR_pin6);

  // Notes on the sheet:
  //   1001 - LDA - ADDR
  //   1010 - WRIT - ADDR, REG (2 bit literal)
  //   LDA LOADS TO REGISTER 3 (11)
  //   1000 - SAV - ADDR, LITERAL
  //   SAV_LINE
  //   LDA_LINE
  //   WRIT_LINE
  //   THIS UNIT ENSURES THAT EXTERNAL INPUT GETS PRIORITY
  //   REPLACE WITH 4072s
endmodule

module COUNTER_8_Bit (
  input  CLK,
  input  RESET,
  input  HI,
  output O7,
  output O6,
  output O5,
  output O4,
  output O3,
  output O2,
  output O1,
  output O0
);

  wire and_1_out, and_2_out, and_3_out, and_4_out, and_5_out, or_1_out, or_2_out, or_3_out, or_4_out,
       or_5_out, or_6_out, or_7_out, or_8_out;

  J_K_Flip_Flop j_k_ff_1 (.J(1'b1), .K(1'b1), .clk(or_1_out), .Q(O7), .reset(RESET));  // open: Qn, preset
  or or_1 (or_1_out, CLK, HI);
  or or_2 (or_2_out, HI, O7);
  J_K_Flip_Flop j_k_ff_2 (.J(or_2_out), .K(or_2_out), .clk(or_1_out), .Q(O6), .reset(RESET));  // open: Qn, preset
  and and_1 (and_1_out, O7, O6);
  J_K_Flip_Flop j_k_ff_3 (.J(or_3_out), .K(or_3_out), .clk(or_1_out), .Q(O5), .reset(RESET));  // open: Qn, preset
  or or_3 (or_3_out, HI, and_1_out);
  and and_2 (and_2_out, O5, and_1_out);
  J_K_Flip_Flop j_k_ff_4 (.J(or_4_out), .K(or_4_out), .clk(or_1_out), .Q(O4), .reset(RESET));  // open: Qn, preset
  or or_4 (or_4_out, HI, and_2_out);
  J_K_Flip_Flop j_k_ff_5 (.J(or_5_out), .K(or_5_out), .clk(or_1_out), .Q(O3), .reset(RESET));  // open: Qn, preset
  or or_5 (or_5_out, HI, and_3_out);
  and and_3 (and_3_out, O4, and_2_out);
  J_K_Flip_Flop j_k_ff_6 (.J(or_6_out), .K(or_6_out), .clk(or_1_out), .Q(O2), .reset(RESET));  // open: Qn, preset
  or or_6 (or_6_out, HI, and_4_out);
  and and_4 (and_4_out, and_3_out, O3);
  and and_5 (and_5_out, O2, and_4_out);
  J_K_Flip_Flop j_k_ff_7 (.J(or_7_out), .K(or_7_out), .clk(or_1_out), .Q(O1), .reset(RESET));  // open: Qn, preset
  or or_7 (or_7_out, HI, and_5_out);
  J_K_Flip_Flop j_k_ff_8 (.J(or_8_out), .K(or_8_out), .clk(or_1_out), .Q(O0), .reset(RESET));  // open: Qn, preset
  or or_8 (or_8_out, HI, O0);
  // AND_Gate and_6 has open pins: in0=and_5_out, in1=O1, out=open
endmodule

module PROGRAM_COUNTER (
  input  OP0,
  input  OP1,
  input  OP2,
  input  OP3,
  input  A_ARG_0,
  input  A_ARG_1,
  input  A_ARG_2,
  input  A_ARG_3,
  input  A_ARG_4,
  input  A_ARG_5,
  input  A_ARG_6,
  input  A_ARG_7,
  input  B_ARG_0,
  input  B_ARG_1,
  input  B_ARD_2,
  input  B_ARG_3,
  input  B_ARG_4,
  input  B_ARG_5,
  input  B_ARG_6,
  input  B_ARG_7
);

  wire clock_1_out, counter_8_bit_1_o2, counter_8_bit_1_o3, counter_8_bit_1_o4, counter_8_bit_1_o5,
       counter_8_bit_1_o6, counter_8_bit_1_o7, CPU_error_bit, CPU_o0, CPU_o1, CPU_o2, CPU_o3, GO_out,
       or_1_out, ram_64_nibble_1_o0, ram_64_nibble_1_o1, ram_64_nibble_1_o2, ram_64_nibble_1_o3,
       ram_64_nibble_2_o0, ram_64_nibble_2_o1, ram_64_nibble_2_o2, ram_64_nibble_2_o3, ram_64_nibble_3_o0,
       ram_64_nibble_3_o1, ram_64_nibble_3_o2, ram_64_nibble_3_o3, ram_64_nibble_4_o0, ram_64_nibble_4_o1,
       ram_64_nibble_4_o2, ram_64_nibble_4_o3, ram_64_nibble_5_o0, ram_64_nibble_5_o1, ram_64_nibble_5_o2,
       ram_64_nibble_5_o3, START_EXECUTION_out;

  Button START_EXECUTION (.out(START_EXECUTION_out));
  or or_1 (or_1_out, clock_1_out, GO_out);
  Clock clock_1 (.out(clock_1_out));
  COUNTER_8_Bit counter_8_bit_1 (
    .CLK(or_1_out), .HI(START_EXECUTION_out), .O7(counter_8_bit_1_o7), .O6(counter_8_bit_1_o6),
    .O5(counter_8_bit_1_o5), .O4(counter_8_bit_1_o4), .O3(counter_8_bit_1_o3), .O2(counter_8_bit_1_o2));  // open: RESET, O1, O0
  Button GO (.out(GO_out));
  RAM_64_Nibble ram_64_nibble_1 (
    .D0(OP0), .D1(OP1), .D2(OP2), .D3(OP3), .A0(counter_8_bit_1_o2), .A1(counter_8_bit_1_o3),
    .A2(counter_8_bit_1_o4), .A3(counter_8_bit_1_o5), .CLK(GO_out), .A4(counter_8_bit_1_o6),
    .A5(counter_8_bit_1_o7), .O0(ram_64_nibble_1_o0), .O1(ram_64_nibble_1_o1), .O2(ram_64_nibble_1_o2),
    .O3(ram_64_nibble_1_o3));
  RAM_64_Nibble ram_64_nibble_2 (
    .D0(A_ARG_0), .D1(A_ARG_1), .D2(A_ARG_2), .D3(A_ARG_3), .A0(counter_8_bit_1_o2), .A1(counter_8_bit_1_o3),
    .A2(counter_8_bit_1_o4), .A3(counter_8_bit_1_o5), .CLK(GO_out), .A4(counter_8_bit_1_o6),
    .A5(counter_8_bit_1_o7), .O0(ram_64_nibble_2_o0), .O1(ram_64_nibble_2_o1), .O2(ram_64_nibble_2_o2),
    .O3(ram_64_nibble_2_o3));
  RAM_64_Nibble ram_64_nibble_3 (
    .D0(A_ARG_4), .D1(A_ARG_5), .D2(A_ARG_6), .D3(A_ARG_7), .A0(counter_8_bit_1_o2), .A1(counter_8_bit_1_o3),
    .A2(counter_8_bit_1_o4), .A3(counter_8_bit_1_o5), .CLK(GO_out), .A4(counter_8_bit_1_o6),
    .A5(counter_8_bit_1_o7), .O0(ram_64_nibble_3_o0), .O1(ram_64_nibble_3_o1), .O2(ram_64_nibble_3_o2),
    .O3(ram_64_nibble_3_o3));
  RAM_64_Nibble ram_64_nibble_4 (
    .D0(B_ARG_0), .D1(B_ARG_1), .D2(B_ARD_2), .D3(B_ARG_3), .A0(counter_8_bit_1_o2), .A1(counter_8_bit_1_o3),
    .A2(counter_8_bit_1_o4), .A3(counter_8_bit_1_o5), .CLK(GO_out), .A4(counter_8_bit_1_o6),
    .A5(counter_8_bit_1_o7), .O0(ram_64_nibble_4_o0), .O1(ram_64_nibble_4_o1), .O2(ram_64_nibble_4_o2),
    .O3(ram_64_nibble_4_o3));
  RAM_64_Nibble ram_64_nibble_5 (
    .D0(B_ARG_4), .D1(B_ARG_5), .D2(B_ARG_6), .D3(B_ARG_7), .A0(counter_8_bit_1_o2), .A1(counter_8_bit_1_o3),
    .A2(counter_8_bit_1_o4), .A3(counter_8_bit_1_o5), .CLK(GO_out), .A4(counter_8_bit_1_o6),
    .A5(counter_8_bit_1_o7), .O0(ram_64_nibble_5_o0), .O1(ram_64_nibble_5_o1), .O2(ram_64_nibble_5_o2),
    .O3(ram_64_nibble_5_o3));
  LED led_1 (.in(CPU_o0));
  CONTROL CPU (
    .GO(clock_1_out), .OP0(ram_64_nibble_1_o0), .OP1(ram_64_nibble_1_o1), .OP2(ram_64_nibble_1_o2),
    .OP3(ram_64_nibble_1_o3), .A_ARG_0(ram_64_nibble_2_o0), .A_ARG_1(ram_64_nibble_2_o1),
    .A_ARG_2(ram_64_nibble_2_o2), .A_ARG_3(ram_64_nibble_2_o3), .A_ARG_4(ram_64_nibble_3_o0),
    .A_ARG_5(ram_64_nibble_3_o1), .A_ARG_6(ram_64_nibble_3_o2), .A_ARG_7(ram_64_nibble_3_o3),
    .B_ARG_0(ram_64_nibble_4_o0), .B_ARG_1(ram_64_nibble_4_o1), .B_ARD_2(ram_64_nibble_4_o2),
    .B_ARG_3(ram_64_nibble_4_o3), .B_ARG_4(ram_64_nibble_5_o0), .B_ARG_5(ram_64_nibble_5_o1),
    .B_ARG_6(ram_64_nibble_5_o2), .B_ARG_7(ram_64_nibble_5_o3), .O0(CPU_o0), .O1(CPU_o1), .O2(CPU_o2),
    .O3(CPU_o3), .ERROR_BIT(CPU_error_bit));
  LED led_2 (.in(CPU_o1));
  LED led_3 (.in(CPU_o2));
  LED led_4 (.in(CPU_o3));
  LED led_5 (.in(CPU_error_bit));

  // Notes on the sheet:
  //   001 - SUB - LITERAL, LITERAL
  //   010 - NOP - IGNORED x2
  //   011 - NOP - IGNORED x2
  //   101 - XOR - LITERAL, LITERAL
  //   110 - OR - LITERAL, LITERAL
  //   1000 - SAV - LITERAL, ADDR
  //   1001 - MOV - ADDR, ADDR
  //   000 - ADD - LITERAL, LITERAL
  //   100 - NOT - LITERAL, IGNORED
  //   111 - AND - LITERAL, LITERAL
  //   The inputs are for programming mode - the op is written  to the next address.
endmodule

module program_memory (
  input  CLK,
  input  RESET,
  input  HI,
  input  in_4,
  input  [3:0] OP,
  input  [7:0] A_ARG,
  input  [7:0] B_ARG,
  output O7,
  output O6,
  output O5,
  output O4,
  output O3,
  output O2,
  output O1,
  output O0,
  output OUTPIN,
  output [3:0] out_17,
  output [7:0] out_18,
  output [7:0] out_19
);

  wire and_1_out, and_2_out, and_3_out, and_4_out, and_5_out, button_1_out, clock_1_out, GO_out, not_1_out,
       or_1_out, or_2_out, or_3_out, or_4_out, or_5_out, or_6_out, or_7_out, or_8_out, or_9_out,
       START_EXECUTION_out;
  wire [5:0] counter_8_bit_1_o7;

  or or_1 (or_1_out, CLK, HI);
  J_K_Flip_Flop j_k_ff_1 (.J(1'b1), .K(1'b1), .clk(or_1_out), .Q(O7), .reset(RESET));  // open: Qn, preset
  Button START_EXECUTION (.out(START_EXECUTION_out));
  or or_2 (or_2_out, clock_1_out, GO_out);
  Button button_1 (.out(button_1_out));
  J_K_Flip_Flop j_k_ff_2 (.J(or_3_out), .K(or_3_out), .clk(or_1_out), .Q(O6), .reset(RESET));  // open: Qn, preset
  or or_3 (or_3_out, HI, O7);
  Clock clock_1 (.out(clock_1_out));
  COUNTER_8_Bit counter_8_bit_1 (
    .CLK(or_2_out), .RESET(button_1_out), .HI(START_EXECUTION_out), .O7(counter_8_bit_1_o7[0]),
    .O6(counter_8_bit_1_o7[1]), .O5(counter_8_bit_1_o7[2]), .O4(counter_8_bit_1_o7[3]),
    .O3(counter_8_bit_1_o7[4]), .O2(counter_8_bit_1_o7[5]));  // open: O1, O0
  and and_1 (and_1_out, O7, O6);
  J_K_Flip_Flop j_k_ff_3 (.J(or_4_out), .K(or_4_out), .clk(or_1_out), .Q(O5), .reset(RESET));  // open: Qn, preset
  or or_4 (or_4_out, HI, and_1_out);
  J_K_Flip_Flop j_k_ff_4 (.J(or_5_out), .K(or_5_out), .clk(or_1_out), .Q(O4), .reset(RESET));  // open: Qn, preset
  or or_5 (or_5_out, HI, and_2_out);
  Button GO (.out(GO_out));
  and and_2 (and_2_out, O5, and_1_out);
  and and_3 (and_3_out, O4, and_2_out);
  J_K_Flip_Flop j_k_ff_5 (.J(or_6_out), .K(or_6_out), .clk(or_1_out), .Q(O3), .reset(RESET));  // open: Qn, preset
  or or_6 (or_6_out, HI, and_3_out);
  or or_7 (or_7_out, HI, and_4_out);
  and and_4 (and_4_out, and_3_out, O3);
  J_K_Flip_Flop j_k_ff_6 (.J(or_7_out), .K(or_7_out), .clk(or_1_out), .Q(O2), .reset(RESET));  // open: Qn, preset
  RAM #(.addrWidth(6), .dataWidth(4)) ram_1 (
    .addr(counter_8_bit_1_o7), .we(GO_out), .oe(1'b1), .clk(or_2_out), .din(OP), .dout(out_17));
  RAM #(.addrWidth(6)) ram_2 (
    .addr(counter_8_bit_1_o7), .we(GO_out), .oe(1'b1), .clk(or_2_out), .din(A_ARG), .dout(out_18));
  RAM #(.addrWidth(6)) ram_3 (
    .addr(counter_8_bit_1_o7), .we(GO_out), .oe(1'b1), .clk(or_2_out), .din(B_ARG), .dout(out_19));
  J_K_Flip_Flop j_k_ff_7 (.J(or_8_out), .K(or_8_out), .clk(or_1_out), .Q(O1), .reset(RESET));  // open: Qn, preset
  or or_8 (or_8_out, HI, and_5_out);
  not not_1 (not_1_out, in_4);
  and and_5 (and_5_out, O2, and_4_out);
  // AND_Gate and_6 has open pins: in0=and_5_out, in1=O1, out=open
  J_K_Flip_Flop j_k_ff_8 (.J(or_9_out), .K(or_9_out), .clk(or_1_out), .Q(O0), .reset(RESET));  // open: Qn, preset
  or or_9 (or_9_out, HI, O0);
  and and_7 (OUTPIN, in_4, not_1_out);

  // Notes on the sheet:
  //   HM6116L
  //   000 - ADD - LITERAL, LITERAL
  //   001 - SUB - LITERAL, LITERAL
  //   010 - NOP - IGNORED x2
  //   011 - NOP - IGNORED x2
  //   100 - NOT - LITERAL, IGNORED
  //   101 - XOR - LITERAL, LITERAL
  //   110 - OR - LITERAL, LITERAL
  //   111 - AND - LITERAL, LITERAL
  //   1000 - SAV - LITERAL, ADDR
  //   1001 - MOV - ADDR, ADDR
  //   The inputs are for programming mode - the op is written  to the next address.
endmodule

module new_main (
  input  OP0,
  input  OP1,
  input  OP2,
  input  A_ARG_0,
  input  OP3,
  input  A_ARG_1,
  input  A_ARG_2,
  input  A_ARG_3,
  input  A_ARG_4,
  input  A_ARG_5,
  input  A_ARG_6,
  input  A_ARG_7,
  input  B_ARG_0,
  input  B_ARG_1,
  input  B_ARG_2,
  input  B_ARG_3,
  input  B_ARG_4,
  input  B_ARG_5,
  input  B_ARG_6,
  input  B_ARG_7,
  input  GO,
  output O1,
  output O0,
  output O2,
  output O3,
  output ERROR_OR_CARRY,
  output o3_7432,
  output o2_7432,
  output o1_7432,
  output o0_7432
);

  wire ADDER_CHIP_pin1, ADDER_CHIP_pin4, ADDER_CHIP_pin7, ADDER_CHIP_pin9, ADDER_CHIP_pin10,
       ADDER_CHIP_pin13, ADDER_SIGNAL_CHECKERS_pin2, AND_CHIP_pin3, AND_CHIP_pin6, AND_CHIP_pin8,
       AND_CHIP_pin11, AND_SIGNAL_CHECKERS_pin2, AND_SIGNAL_CHECKERS_pin3, AND_SIGNAL_CHECKERS_pin6,
       AND_SIGNAL_CHECKERS_pin8, AND_SIGNAL_CHECKERS_pin11, ARITHEMETIC_GENERAL_OUTPUT_SIGNAL_CHECKER_pin3,
       ARITHEMETIC_GENERAL_OUTPUT_SIGNAL_CHECKER_pin6, ARITHEMETIC_GENERAL_OUTPUT_SIGNAL_CHECKER_pin8,
       ARITHEMETIC_GENERAL_OUTPUT_SIGNAL_CHECKER_pin11, DATA_IN_ACCUMULATOR_pin2, DATA_IN_ACCUMULATOR_pin5,
       DATA_IN_ACCUMULATOR_pin9, DATA_IN_ACCUMULATOR_pin12, DATA_NEGATER_pin3, DATA_NEGATER_pin6,
       DATA_NEGATER_pin8, DATA_NEGATER_pin11, dip_7425_1_p5, ERROR_OR_CARRY_SIGNAL_CHECKER_pin3,
       ERROR_OR_CARRY_SIGNAL_CHECKER_pin11, LOGIC_BIT_SET_CHECKER_pin3, LOGIC_BIT_SET_CHECKER_pin6,
       LOGIC_BIT_SET_CHECKER_pin8, n7400_1_pin8, n7400_1_pin11, n7400_2_pin6, n7400_2_pin8, n7400_2_pin11,
       n7408_1_pin8, n7408_2_pin8, n7408_2_pin9, n7408_3_pin8, n7408_3_pin9, n7408_4_pin3, n7408_4_pin6,
       n7408_4_pin8, n7408_4_pin11, n7421_1_pin1, n7421_1_pin6, n7432_2_pin3, n7432_2_pin6, n7432_2_pin8,
       n7432_2_pin10, n7432_3_pin2, n7432_3_pin3, n7432_3_pin11, NOT_CHIP_pin3, NOT_CHIP_pin6, NOT_CHIP_pin8,
       NOT_CHIP_pin11, NOT_SIGNAL_CHECKERS_pin3, NOT_SIGNAL_CHECKERS_pin6, NOT_SIGNAL_CHECKERS_pin8,
       NOT_SIGNAL_CHECKERS_pin11, O0_ACCUMULATOR_out, O1_ACCUMULATOR_out, O2_ACCUMULATOR_out,
       O3_ACCUMULATOR_out, OP_INPUT_CHECKER_HI_BIT_pin6, OP_INPUT_CHECKER_LO_3_BITS_pin6,
       OP_INPUT_CHECKER_LO_3_BITS_pin12, OP_INPUT_NEGATER_pin3, OP_INPUT_NEGATER_pin8,
       OP_INPUT_NEGATER_pin11, OPCODE_CHECKER_INPUT_GENERATOR_pin3, OPCODE_CHECKER_INPUT_GENERATOR_pin6,
       OPCODE_CHECKER_INPUT_GENERATOR_pin8, OPCODE_CHECKER_INPUT_GENERATOR_pin11, OPCODE_NEGATERS_pin3,
       OPCODE_NEGATERS_pin6, OPCODE_NEGATERS_pin8, OPCODE_NEGATERS_pin11, OPCODE_SELECTOR_pin3,
       OPCODE_SELECTOR_pin6, OPCODE_SELECTOR_pin8, OPCODE_SELECTOR_pin11, OR_CHIP_pin3, OR_CHIP_pin6,
       OR_CHIP_pin8, OR_CHIP_pin11, OR_SIGNAL_CHECKERS_pin3, OR_SIGNAL_CHECKERS_pin6,
       OR_SIGNAL_CHECKERS_pin8, OR_SIGNAL_CHECKERS_pin11, OVERWRITE_CHECKER_ON_NEGATED_DATA_pin3,
       OVERWRITE_CHECKER_ON_NEGATED_DATA_pin6, OVERWRITE_CHECKER_ON_NEGATED_DATA_pin8,
       OVERWRITE_CHECKER_ON_NEGATED_DATA_pin11, REGISTER_00_ACCUMULATOR_pin3, REGISTER_00_ACCUMULATOR_pin6,
       REGISTER_00_ACCUMULATOR_pin8, REGISTER_00_ACCUMULATOR_pin11, REGISTER_01_ACCUMULATOR_pin3,
       REGISTER_01_ACCUMULATOR_pin6, REGISTER_01_ACCUMULATOR_pin8, REGISTER_01_ACCUMULATOR_pin11,
       REGISTER_10_ACCUMULATOR_pin3, REGISTER_10_ACCUMULATOR_pin6, REGISTER_10_ACCUMULATOR_pin8,
       REGISTER_10_ACCUMULATOR_pin11, REGISTER_11_ACCUMULATOR_pin3, REGISTER_11_ACCUMULATOR_pin6,
       REGISTER_11_ACCUMULATOR_pin8, REGISTER_11_ACCUMULATOR_pin11, REGISTER_OUT_CHECKERS_pin1,
       REGISTER_OUT_CHECKERS_pin2, REGISTER_OUT_CHECKERS_pin5, REGISTER_OUT_CHECKERS_pin10,
       REGISTER_OUT_CHECKERS_pin12, REGISTER_SELECTOR_NEGATER_pin3, REGISTER_SELECTOR_NEGATER_pin6,
       REGISTER_SELECTOR_pin3, REGISTER_SELECTOR_pin6, REGISTER_SELECTOR_pin8, REGISTER_SELECTOR_pin11,
       REGISTER_WRITER_pin6, REGISTER_WRITER_pin8, REGISTER_WRITER_pin11, SAV_LITERAL_CHECKER_pin1,
       SAV_LITERAL_CHECKER_pin3, SAV_LITERAL_CHECKER_pin6, SAV_LITERAL_CHECKER_pin8,
       SAV_LITERAL_CHECKER_pin11, SUBTRACTER_CHIP_pin1, SUBTRACTER_CHIP_pin4, SUBTRACTER_CHIP_pin7,
       SUBTRACTER_CHIP_pin9, SUBTRACTER_CHIP_pin10, SUBTRACTER_CHIP_pin13, SUBTRACTER_INPUT_NEGATER_pin3,
       SUBTRACTER_INPUT_NEGATER_pin6, SUBTRACTER_INPUT_NEGATER_pin8, SUBTRACTER_INPUT_NEGATER_pin11,
       SUBTRACTER_SIGNAL_CHECKERS_pin3, SUBTRACTER_SIGNAL_CHECKERS_pin6, SUBTRACTER_SIGNAL_CHECKERS_pin8,
       SUBTRACTER_SIGNAL_CHECKERS_pin11, WRITE_AND_OUTPUT_ACCUMULATORS_pin3,
       WRITE_AND_OUTPUT_ACCUMULATORS_pin6, WRITE_AND_OUTPUT_ACCUMULATORS_pin11, XOR_CHIP_pin3, XOR_CHIP_pin6,
       XOR_CHIP_pin8, XOR_CHIP_pin11, XOR_SIGNAL_CHECKERS_pin3, XOR_SIGNAL_CHECKERS_pin6,
       XOR_SIGNAL_CHECKERS_pin8, XOR_SIGNAL_CHECKERS_pin11;
  wire [3:0] ADDER_CHIP_pin5, DATA_IN_ACCUMULATOR_pin11, n7408_4_pin5, n7432_2_pin1, n7432_4_pin6,
       ram_1_dout, register_3_q, register_4_q, SUBTRACTER_INPUT_NEGATER_pin4;

  _7400 u_7400_1 (
    .pin13(OP2), .pin12(OP2), .pin11(n7400_1_pin11), .pin10(OP3), .pin9(OP3), .pin8(n7400_1_pin8));  // open: pin1, pin2, pin3, pin4, pin5, pin6
  _7400 SUBTRACTER_INPUT_NEGATER (
    .pin1(SUBTRACTER_INPUT_NEGATER_pin4[1]), .pin2(SUBTRACTER_INPUT_NEGATER_pin4[1]),
    .pin3(SUBTRACTER_INPUT_NEGATER_pin3), .pin4(SUBTRACTER_INPUT_NEGATER_pin4[0]),
    .pin5(SUBTRACTER_INPUT_NEGATER_pin4[0]), .pin6(SUBTRACTER_INPUT_NEGATER_pin6),
    .pin13(SUBTRACTER_INPUT_NEGATER_pin4[3]), .pin12(SUBTRACTER_INPUT_NEGATER_pin4[3]),
    .pin11(SUBTRACTER_INPUT_NEGATER_pin11), .pin10(SUBTRACTER_INPUT_NEGATER_pin4[2]),
    .pin9(SUBTRACTER_INPUT_NEGATER_pin4[2]), .pin8(SUBTRACTER_INPUT_NEGATER_pin8));
  _7408 OPCODE_SELECTOR (
    .pin1(n7400_1_pin8), .pin2(n7400_1_pin11), .pin3(OPCODE_SELECTOR_pin3), .pin4(n7400_1_pin11), .pin5(OP3),
    .pin6(OPCODE_SELECTOR_pin6), .pin13(OP2), .pin12(n7400_1_pin8), .pin11(OPCODE_SELECTOR_pin11),
    .pin10(OP3), .pin9(OP2), .pin8(OPCODE_SELECTOR_pin8));
  _7408 SAV_LITERAL_CHECKER (
    .pin1(SAV_LITERAL_CHECKER_pin1), .pin2(B_ARG_5), .pin3(SAV_LITERAL_CHECKER_pin3),
    .pin4(SAV_LITERAL_CHECKER_pin1), .pin5(B_ARG_4), .pin6(SAV_LITERAL_CHECKER_pin6),
    .pin13(SAV_LITERAL_CHECKER_pin1), .pin12(B_ARG_7), .pin11(SAV_LITERAL_CHECKER_pin11),
    .pin10(SAV_LITERAL_CHECKER_pin1), .pin9(B_ARG_6), .pin8(SAV_LITERAL_CHECKER_pin8));
  _7400 u_7400_2 (
    .pin4(OP1), .pin5(OP1), .pin6(n7400_2_pin6), .pin13(OP3), .pin12(OP3), .pin11(n7400_2_pin11),
    .pin10(OP1), .pin9(OP1), .pin8(n7400_2_pin8));  // open: pin1, pin2, pin3
  _7421 u_7421_1 (
    .pin1(n7421_1_pin1), .pin2(n7421_1_pin1), .pin4(GO), .pin5(GO), .pin6(n7421_1_pin6),
    .pin13(n7400_2_pin6), .pin12(n7400_2_pin8), .pin10(OP2), .pin9(n7400_2_pin11), .pin8(n7421_1_pin1));  // open: pin3, pin11
  _7408 AND_CHIP (
    .pin1(ADDER_CHIP_pin5[3]), .pin2(SUBTRACTER_INPUT_NEGATER_pin4[3]), .pin3(AND_CHIP_pin3),
    .pin4(ADDER_CHIP_pin5[2]), .pin5(SUBTRACTER_INPUT_NEGATER_pin4[2]), .pin6(AND_CHIP_pin6),
    .pin13(ADDER_CHIP_pin5[1]), .pin12(SUBTRACTER_INPUT_NEGATER_pin4[1]), .pin11(AND_CHIP_pin11),
    .pin10(ADDER_CHIP_pin5[3]), .pin9(SUBTRACTER_INPUT_NEGATER_pin4[0]), .pin8(AND_CHIP_pin8));
  _74283 ADDER_CHIP (
    .pin1(ADDER_CHIP_pin1), .pin2(ADDER_CHIP_pin5[1]), .pin3(SUBTRACTER_INPUT_NEGATER_pin4[1]),
    .pin4(ADDER_CHIP_pin4), .pin5(ADDER_CHIP_pin5[0]), .pin6(SUBTRACTER_INPUT_NEGATER_pin4[0]),
    .pin7(ADDER_CHIP_pin7), .pin15(SUBTRACTER_INPUT_NEGATER_pin4[2]), .pin14(ADDER_CHIP_pin5[2]),
    .pin13(ADDER_CHIP_pin13), .pin12(SUBTRACTER_INPUT_NEGATER_pin4[3]), .pin11(ADDER_CHIP_pin5[3]),
    .pin10(ADDER_CHIP_pin10), .pin9(ADDER_CHIP_pin9));
  _7400 OP_INPUT_NEGATER (
    .pin1(OP2), .pin2(OP2), .pin3(OP_INPUT_NEGATER_pin3), .pin13(OP1), .pin12(OP1),
    .pin11(OP_INPUT_NEGATER_pin11), .pin10(OP3), .pin9(OP3), .pin8(OP_INPUT_NEGATER_pin8));  // open: pin4, pin5, pin6
  _7411 OP_INPUT_CHECKER_LO_3_BITS (
    .pin1(OP_INPUT_NEGATER_pin11), .pin2(OP_INPUT_NEGATER_pin8), .pin3(OP3), .pin4(OP_INPUT_NEGATER_pin3),
    .pin5(OP_INPUT_NEGATER_pin11), .pin6(OP_INPUT_CHECKER_LO_3_BITS_pin6), .pin13(OP_INPUT_NEGATER_pin3),
    .pin12(OP_INPUT_CHECKER_LO_3_BITS_pin12));  // open: pin11, pin10, pin9, pin8
  _7408 AND_SIGNAL_CHECKERS (
    .pin1(AND_CHIP_pin8), .pin2(AND_SIGNAL_CHECKERS_pin2), .pin3(AND_SIGNAL_CHECKERS_pin3),
    .pin4(AND_CHIP_pin11), .pin5(AND_SIGNAL_CHECKERS_pin2), .pin6(AND_SIGNAL_CHECKERS_pin6),
    .pin13(AND_CHIP_pin3), .pin12(AND_SIGNAL_CHECKERS_pin2), .pin11(AND_SIGNAL_CHECKERS_pin11),
    .pin10(AND_CHIP_pin6), .pin9(AND_SIGNAL_CHECKERS_pin2), .pin8(AND_SIGNAL_CHECKERS_pin8));
  _7400 OPCODE_NEGATERS (
    .pin1(OP1), .pin2(OP1), .pin3(OPCODE_NEGATERS_pin3), .pin4(OP0), .pin5(OP0), .pin6(OPCODE_NEGATERS_pin6),
    .pin13(OP3), .pin12(OP3), .pin11(OPCODE_NEGATERS_pin11), .pin10(OP2), .pin9(OP2),
    .pin8(OPCODE_NEGATERS_pin8));
  _74283 SUBTRACTER_CHIP (
    .pin1(SUBTRACTER_CHIP_pin1), .pin2(ADDER_CHIP_pin5[1]), .pin3(SUBTRACTER_INPUT_NEGATER_pin3),
    .pin4(SUBTRACTER_CHIP_pin4), .pin5(ADDER_CHIP_pin5[0]), .pin6(SUBTRACTER_INPUT_NEGATER_pin6),
    .pin7(SUBTRACTER_CHIP_pin7), .pin15(SUBTRACTER_INPUT_NEGATER_pin8), .pin14(ADDER_CHIP_pin5[2]),
    .pin13(SUBTRACTER_CHIP_pin13), .pin12(SUBTRACTER_INPUT_NEGATER_pin11), .pin11(ADDER_CHIP_pin5[3]),
    .pin10(SUBTRACTER_CHIP_pin10), .pin9(SUBTRACTER_CHIP_pin9));
  _7408 LOGIC_BIT_SET_CHECKER (
    .pin1(OPCODE_SELECTOR_pin6), .pin2(OP1), .pin3(LOGIC_BIT_SET_CHECKER_pin3), .pin4(OPCODE_SELECTOR_pin3),
    .pin5(OP1), .pin6(LOGIC_BIT_SET_CHECKER_pin6), .pin13(OP1), .pin12(OPCODE_SELECTOR_pin8),
    .pin11(AND_SIGNAL_CHECKERS_pin2), .pin10(OP1), .pin9(OPCODE_SELECTOR_pin11),
    .pin8(LOGIC_BIT_SET_CHECKER_pin8));
  _7432 OR_CHIP (
    .pin1(ADDER_CHIP_pin5[3]), .pin2(SUBTRACTER_INPUT_NEGATER_pin4[3]), .pin3(OR_CHIP_pin3),
    .pin4(ADDER_CHIP_pin5[2]), .pin5(SUBTRACTER_INPUT_NEGATER_pin4[2]), .pin6(OR_CHIP_pin6),
    .pin13(ADDER_CHIP_pin5[1]), .pin12(SUBTRACTER_INPUT_NEGATER_pin4[1]), .pin11(OR_CHIP_pin11),
    .pin10(ADDER_CHIP_pin5[3]), .pin9(SUBTRACTER_INPUT_NEGATER_pin4[0]), .pin8(OR_CHIP_pin8));
  _7408 ADDER_SIGNAL_CHECKERS (
    .pin1(ADDER_CHIP_pin1), .pin2(ADDER_SIGNAL_CHECKERS_pin2), .pin3(o2_7432), .pin4(ADDER_CHIP_pin4),
    .pin5(ADDER_SIGNAL_CHECKERS_pin2), .pin6(o3_7432), .pin13(ADDER_CHIP_pin10),
    .pin12(ADDER_SIGNAL_CHECKERS_pin2), .pin11(o0_7432), .pin10(ADDER_CHIP_pin13),
    .pin9(ADDER_SIGNAL_CHECKERS_pin2), .pin8(o1_7432));
  _7432 DATA_IN_ACCUMULATOR (
    .pin1(SAV_LITERAL_CHECKER_pin3), .pin2(DATA_IN_ACCUMULATOR_pin2), .pin3(DATA_IN_ACCUMULATOR_pin11[2]),
    .pin4(SAV_LITERAL_CHECKER_pin6), .pin5(DATA_IN_ACCUMULATOR_pin5), .pin6(DATA_IN_ACCUMULATOR_pin11[3]),
    .pin13(SAV_LITERAL_CHECKER_pin11), .pin12(DATA_IN_ACCUMULATOR_pin12),
    .pin11(DATA_IN_ACCUMULATOR_pin11[0]), .pin10(SAV_LITERAL_CHECKER_pin8), .pin9(DATA_IN_ACCUMULATOR_pin9),
    .pin8(DATA_IN_ACCUMULATOR_pin11[1]));
  _7408 REGISTER_OUT_CHECKERS (
    .pin1(REGISTER_OUT_CHECKERS_pin1), .pin2(REGISTER_OUT_CHECKERS_pin2), .pin3(DATA_IN_ACCUMULATOR_pin9),
    .pin4(REGISTER_OUT_CHECKERS_pin1), .pin5(REGISTER_OUT_CHECKERS_pin5), .pin6(DATA_IN_ACCUMULATOR_pin12),
    .pin13(REGISTER_OUT_CHECKERS_pin1), .pin12(REGISTER_OUT_CHECKERS_pin12),
    .pin11(DATA_IN_ACCUMULATOR_pin5), .pin10(REGISTER_OUT_CHECKERS_pin10), .pin9(REGISTER_OUT_CHECKERS_pin1),
    .pin8(DATA_IN_ACCUMULATOR_pin2));
  _7408 OP_INPUT_CHECKER_HI_BIT (
    .pin1(OP_INPUT_CHECKER_LO_3_BITS_pin12), .pin2(OP0), .pin3(SAV_LITERAL_CHECKER_pin1),
    .pin4(OP_INPUT_CHECKER_LO_3_BITS_pin6), .pin5(OP0), .pin6(OP_INPUT_CHECKER_HI_BIT_pin6), .pin13(OP2),
    .pin12(OP_INPUT_NEGATER_pin8), .pin11(REGISTER_OUT_CHECKERS_pin1));  // open: pin10, pin9, pin8
  _7408 OR_SIGNAL_CHECKERS (
    .pin1(OR_CHIP_pin11), .pin2(LOGIC_BIT_SET_CHECKER_pin8), .pin3(OR_SIGNAL_CHECKERS_pin3),
    .pin4(OR_CHIP_pin8), .pin5(LOGIC_BIT_SET_CHECKER_pin8), .pin6(OR_SIGNAL_CHECKERS_pin6),
    .pin13(OR_CHIP_pin3), .pin12(LOGIC_BIT_SET_CHECKER_pin8), .pin11(OR_SIGNAL_CHECKERS_pin11),
    .pin10(OR_CHIP_pin6), .pin9(LOGIC_BIT_SET_CHECKER_pin8), .pin8(OR_SIGNAL_CHECKERS_pin8));
  _7408 OPCODE_CHECKER_INPUT_GENERATOR (
    .pin1(OPCODE_NEGATERS_pin3), .pin2(OP3), .pin3(OPCODE_CHECKER_INPUT_GENERATOR_pin3),
    .pin4(OPCODE_NEGATERS_pin3), .pin5(OPCODE_CHECKER_INPUT_GENERATOR_pin3),
    .pin6(OPCODE_CHECKER_INPUT_GENERATOR_pin6), .pin13(OPCODE_NEGATERS_pin8), .pin12(OPCODE_NEGATERS_pin11),
    .pin11(OPCODE_CHECKER_INPUT_GENERATOR_pin11), .pin10(OPCODE_NEGATERS_pin3),
    .pin9(OPCODE_CHECKER_INPUT_GENERATOR_pin11), .pin8(OPCODE_CHECKER_INPUT_GENERATOR_pin8));
  _7408 u_7408_1 (
    .pin13(OPCODE_NEGATERS_pin6), .pin12(OPCODE_CHECKER_INPUT_GENERATOR_pin8),
    .pin11(ADDER_SIGNAL_CHECKERS_pin2), .pin10(OPCODE_NEGATERS_pin6),
    .pin9(OPCODE_CHECKER_INPUT_GENERATOR_pin6), .pin8(n7408_1_pin8));  // open: pin1, pin2, pin3, pin4, pin5, pin6
  _7432 WRITE_AND_OUTPUT_ACCUMULATORS (
    .pin1(GO), .pin2(OP_INPUT_CHECKER_HI_BIT_pin6), .pin3(WRITE_AND_OUTPUT_ACCUMULATORS_pin3),
    .pin4(WRITE_AND_OUTPUT_ACCUMULATORS_pin3), .pin5(REGISTER_OUT_CHECKERS_pin1),
    .pin6(WRITE_AND_OUTPUT_ACCUMULATORS_pin6), .pin13(REGISTER_OUT_CHECKERS_pin1),
    .pin12(SAV_LITERAL_CHECKER_pin1), .pin11(WRITE_AND_OUTPUT_ACCUMULATORS_pin11));  // open: pin10, pin9, pin8
  RAM #(.dataWidth(4)) ram_1 (
    .addr({A_ARG_0, A_ARG_1, A_ARG_2, A_ARG_3, A_ARG_4, A_ARG_5, A_ARG_6, A_ARG_7}),
    .we(WRITE_AND_OUTPUT_ACCUMULATORS_pin11), .oe(WRITE_AND_OUTPUT_ACCUMULATORS_pin6), .clk(GO),
    .din(DATA_IN_ACCUMULATOR_pin11), .dout(ram_1_dout));
  _7486 XOR_CHIP (
    .pin1(ADDER_CHIP_pin5[3]), .pin2(SUBTRACTER_INPUT_NEGATER_pin4[3]), .pin3(XOR_CHIP_pin3),
    .pin4(ADDER_CHIP_pin5[2]), .pin5(SUBTRACTER_INPUT_NEGATER_pin4[2]), .pin6(XOR_CHIP_pin6),
    .pin13(ADDER_CHIP_pin5[1]), .pin12(SUBTRACTER_INPUT_NEGATER_pin4[1]), .pin11(XOR_CHIP_pin11),
    .pin10(ADDER_CHIP_pin5[3]), .pin9(SUBTRACTER_INPUT_NEGATER_pin4[0]), .pin8(XOR_CHIP_pin8));
  _7408 u_7408_2 (
    .pin10(GO), .pin9(n7408_2_pin9), .pin8(n7408_2_pin8));  // open: pin1, pin2, pin3, pin4, pin5, pin6, pin13, pin12, pin11
  _7408 u_7408_3 (
    .pin10(GO), .pin9(n7408_3_pin9), .pin8(n7408_3_pin8));  // open: pin1, pin2, pin3, pin4, pin5, pin6, pin13, pin12, pin11
  _7408 SUBTRACTER_SIGNAL_CHECKERS (
    .pin1(n7408_1_pin8), .pin2(SUBTRACTER_CHIP_pin1), .pin3(SUBTRACTER_SIGNAL_CHECKERS_pin3),
    .pin4(n7408_1_pin8), .pin5(SUBTRACTER_CHIP_pin4), .pin6(SUBTRACTER_SIGNAL_CHECKERS_pin6),
    .pin13(n7408_1_pin8), .pin12(SUBTRACTER_CHIP_pin10), .pin11(SUBTRACTER_SIGNAL_CHECKERS_pin11),
    .pin10(n7408_1_pin8), .pin9(SUBTRACTER_CHIP_pin13), .pin8(SUBTRACTER_SIGNAL_CHECKERS_pin8));
  _7432 u_7432_1 (
    .pin10(n7421_1_pin6), .pin9(OP_INPUT_CHECKER_HI_BIT_pin6), .pin8(n7408_2_pin9));  // open: pin1, pin2, pin3, pin4, pin5, pin6, pin13, pin12, pin11
  _7400 DATA_NEGATER (
    .pin1(ram_1_dout[2]), .pin2(ram_1_dout[2]), .pin3(DATA_NEGATER_pin3), .pin4(ram_1_dout[3]),
    .pin5(ram_1_dout[3]), .pin6(DATA_NEGATER_pin6), .pin13(ram_1_dout[0]), .pin12(ram_1_dout[0]),
    .pin11(DATA_NEGATER_pin11), .pin10(ram_1_dout[1]), .pin9(ram_1_dout[1]), .pin8(DATA_NEGATER_pin8));
  _7400 REGISTER_SELECTOR_NEGATER (
    .pin1(B_ARG_6), .pin2(B_ARG_6), .pin3(REGISTER_SELECTOR_NEGATER_pin3), .pin4(B_ARG_7), .pin5(B_ARG_7),
    .pin6(REGISTER_SELECTOR_NEGATER_pin6));  // open: pin13, pin12, pin11, pin10, pin9, pin8
  _7408 REGISTER_SELECTOR (
    .pin1(B_ARG_6), .pin2(REGISTER_SELECTOR_NEGATER_pin6), .pin3(REGISTER_SELECTOR_pin3), .pin4(B_ARG_6),
    .pin5(B_ARG_7), .pin6(REGISTER_SELECTOR_pin6), .pin13(REGISTER_SELECTOR_NEGATER_pin3),
    .pin12(REGISTER_SELECTOR_NEGATER_pin6), .pin11(REGISTER_SELECTOR_pin11), .pin10(B_ARG_7),
    .pin9(REGISTER_SELECTOR_NEGATER_pin3), .pin8(REGISTER_SELECTOR_pin8));
  _7400 NOT_CHIP (
    .pin1(ADDER_CHIP_pin5[3]), .pin2(ADDER_CHIP_pin5[3]), .pin3(NOT_CHIP_pin3), .pin4(ADDER_CHIP_pin5[3]),
    .pin5(ADDER_CHIP_pin5[3]), .pin6(NOT_CHIP_pin6), .pin13(ADDER_CHIP_pin5[1]), .pin12(ADDER_CHIP_pin5[1]),
    .pin11(NOT_CHIP_pin11), .pin10(ADDER_CHIP_pin5[2]), .pin9(ADDER_CHIP_pin5[2]), .pin8(NOT_CHIP_pin8));
  _7408 XOR_SIGNAL_CHECKERS (
    .pin1(XOR_CHIP_pin6), .pin2(LOGIC_BIT_SET_CHECKER_pin3), .pin3(XOR_SIGNAL_CHECKERS_pin3),
    .pin4(XOR_CHIP_pin3), .pin5(LOGIC_BIT_SET_CHECKER_pin3), .pin6(XOR_SIGNAL_CHECKERS_pin6),
    .pin13(LOGIC_BIT_SET_CHECKER_pin3), .pin12(XOR_CHIP_pin8), .pin11(XOR_SIGNAL_CHECKERS_pin11),
    .pin10(LOGIC_BIT_SET_CHECKER_pin3), .pin9(XOR_CHIP_pin11), .pin8(XOR_SIGNAL_CHECKERS_pin8));
  _7432 u_7432_2 (
    .pin1(n7432_2_pin1[0]), .pin2(n7432_2_pin1[1]), .pin3(n7432_2_pin3), .pin4(n7432_2_pin1[2]),
    .pin5(n7432_2_pin1[3]), .pin6(n7432_2_pin6), .pin13(n7432_2_pin3), .pin12(n7432_2_pin6),
    .pin11(n7408_3_pin9), .pin10(n7432_2_pin10), .pin9(n7408_3_pin8), .pin8(n7432_2_pin8));
  _7408 NOT_SIGNAL_CHECKERS (
    .pin1(NOT_CHIP_pin8), .pin2(LOGIC_BIT_SET_CHECKER_pin6), .pin3(NOT_SIGNAL_CHECKERS_pin3),
    .pin4(NOT_CHIP_pin11), .pin5(LOGIC_BIT_SET_CHECKER_pin6), .pin6(NOT_SIGNAL_CHECKERS_pin6),
    .pin13(NOT_CHIP_pin6), .pin12(LOGIC_BIT_SET_CHECKER_pin6), .pin11(NOT_SIGNAL_CHECKERS_pin11),
    .pin10(LOGIC_BIT_SET_CHECKER_pin6), .pin9(NOT_CHIP_pin3), .pin8(NOT_SIGNAL_CHECKERS_pin8));
  // DIP_7425 dip_7425_1: pin names not known; wires that end beside it: n7432_2_pin1[3], n7432_2_pin1[2], n7432_2_pin1[1], n7432_2_pin1[0], dip_7425_1_p5
  _7432 u_7432_3 (
    .pin1(A_ARG_6), .pin2(n7432_3_pin2), .pin3(n7432_3_pin3), .pin4(A_ARG_5), .pin5(A_ARG_4),
    .pin6(n7432_3_pin2), .pin13(n7432_3_pin3), .pin12(A_ARG_7), .pin11(n7432_3_pin11));  // open: pin10, pin9, pin8
  _7436 OVERWRITE_CHECKER_ON_NEGATED_DATA (
    .pin1(DATA_NEGATER_pin3), .pin2(n7432_3_pin11), .pin3(OVERWRITE_CHECKER_ON_NEGATED_DATA_pin3),
    .pin4(DATA_NEGATER_pin6), .pin5(n7432_3_pin11), .pin6(OVERWRITE_CHECKER_ON_NEGATED_DATA_pin6),
    .pin13(DATA_NEGATER_pin11), .pin12(n7432_3_pin11), .pin11(OVERWRITE_CHECKER_ON_NEGATED_DATA_pin11),
    .pin10(DATA_NEGATER_pin8), .pin9(n7432_3_pin11), .pin8(OVERWRITE_CHECKER_ON_NEGATED_DATA_pin8));
  _7408 REGISTER_WRITER (
    .pin1(REGISTER_SELECTOR_pin3), .pin2(n7408_2_pin8), .pin3(n7432_2_pin10), .pin4(REGISTER_SELECTOR_pin6),
    .pin5(n7408_2_pin8), .pin6(REGISTER_WRITER_pin6), .pin13(REGISTER_SELECTOR_pin11), .pin12(n7408_2_pin8),
    .pin11(REGISTER_WRITER_pin11), .pin10(n7408_2_pin8), .pin9(REGISTER_SELECTOR_pin8),
    .pin8(REGISTER_WRITER_pin8));
  _7408 u_7408_4 (
    .pin1(dip_7425_1_p5), .pin2(n7408_4_pin5[1]), .pin3(n7408_4_pin3), .pin4(dip_7425_1_p5),
    .pin5(n7408_4_pin5[0]), .pin6(n7408_4_pin6), .pin13(dip_7425_1_p5), .pin12(n7408_4_pin5[3]),
    .pin11(n7408_4_pin11), .pin10(dip_7425_1_p5), .pin9(n7408_4_pin5[2]), .pin8(n7408_4_pin8));
  _7408 ERROR_OR_CARRY_SIGNAL_CHECKER (
    .pin1(ADDER_CHIP_pin9), .pin2(OPCODE_CHECKER_INPUT_GENERATOR_pin8),
    .pin3(ERROR_OR_CARRY_SIGNAL_CHECKER_pin3), .pin13(SUBTRACTER_CHIP_pin9),
    .pin12(OPCODE_CHECKER_INPUT_GENERATOR_pin6), .pin11(ERROR_OR_CARRY_SIGNAL_CHECKER_pin11));  // open: pin4, pin5, pin6, pin10, pin9, pin8
  Register #(.width(4)) register_1 (
    .D(n7408_4_pin5), .en(REGISTER_WRITER_pin11), .clk(REGISTER_WRITER_pin11), .Q(ADDER_CHIP_pin5));  // open: clr
  Register #(.width(4)) register_2 (
    .D(n7408_4_pin5), .en(REGISTER_WRITER_pin8), .clk(REGISTER_WRITER_pin8), .Q(SUBTRACTER_INPUT_NEGATER_pin4));  // open: clr
  Register #(.width(4)) register_3 (
    .D(n7432_4_pin6), .en(n7432_2_pin8), .clk(n7432_2_pin8), .Q(register_3_q));  // open: clr
  Register #(.width(4)) register_4 (
    .D(n7408_4_pin5), .en(REGISTER_WRITER_pin6), .clk(REGISTER_WRITER_pin6), .Q(register_4_q));  // open: clr
  or O0_ACCUMULATOR (O0_ACCUMULATOR_out, NOT_SIGNAL_CHECKERS_pin11, XOR_SIGNAL_CHECKERS_pin6, AND_SIGNAL_CHECKERS_pin11, OR_SIGNAL_CHECKERS_pin11);
  or O1_ACCUMULATOR (O1_ACCUMULATOR_out, NOT_SIGNAL_CHECKERS_pin3, XOR_SIGNAL_CHECKERS_pin3, OR_SIGNAL_CHECKERS_pin8, AND_SIGNAL_CHECKERS_pin8);
  or O2_ACCUMULATOR (O2_ACCUMULATOR_out, NOT_SIGNAL_CHECKERS_pin6, XOR_SIGNAL_CHECKERS_pin8, OR_SIGNAL_CHECKERS_pin3, AND_SIGNAL_CHECKERS_pin6);
  or O3_ACCUMULATOR (O3_ACCUMULATOR_out, NOT_SIGNAL_CHECKERS_pin8, XOR_SIGNAL_CHECKERS_pin11, OR_SIGNAL_CHECKERS_pin6, AND_SIGNAL_CHECKERS_pin3);
  _7432 ARITHEMETIC_GENERAL_OUTPUT_SIGNAL_CHECKER (
    .pin1(o1_7432), .pin2(SUBTRACTER_SIGNAL_CHECKERS_pin8),
    .pin3(ARITHEMETIC_GENERAL_OUTPUT_SIGNAL_CHECKER_pin3), .pin4(o0_7432),
    .pin5(SUBTRACTER_SIGNAL_CHECKERS_pin11), .pin6(ARITHEMETIC_GENERAL_OUTPUT_SIGNAL_CHECKER_pin6),
    .pin13(o3_7432), .pin12(SUBTRACTER_SIGNAL_CHECKERS_pin6),
    .pin11(ARITHEMETIC_GENERAL_OUTPUT_SIGNAL_CHECKER_pin11), .pin10(o2_7432),
    .pin9(SUBTRACTER_SIGNAL_CHECKERS_pin3), .pin8(ARITHEMETIC_GENERAL_OUTPUT_SIGNAL_CHECKER_pin8));
  _7432 u_7432_4 (
    .pin1(n7408_4_pin3), .pin2(n7432_2_pin1[1]), .pin3(n7432_4_pin6[1]), .pin4(n7408_4_pin6),
    .pin5(n7432_2_pin1[0]), .pin6(n7432_4_pin6[0]), .pin13(n7408_4_pin11), .pin12(n7432_2_pin1[3]),
    .pin11(n7432_4_pin6[3]), .pin10(n7408_4_pin8), .pin9(n7432_2_pin1[2]), .pin8(n7432_4_pin6[2]));
  _7432 ERROR_OR_CARRY_ACCUMULATOR (
    .pin1(ERROR_OR_CARRY_SIGNAL_CHECKER_pin3), .pin2(ERROR_OR_CARRY_SIGNAL_CHECKER_pin11),
    .pin3(ERROR_OR_CARRY));  // open: pin4, pin5, pin6, pin13, pin12, pin11, pin10, pin9, pin8
  _7432 EXTERNAL_OR_INTERNAL_INPUT_ACCUMULATORS (
    .pin1(OVERWRITE_CHECKER_ON_NEGATED_DATA_pin8), .pin2(A_ARG_6), .pin3(n7408_4_pin5[1]), .pin4(A_ARG_7),
    .pin5(OVERWRITE_CHECKER_ON_NEGATED_DATA_pin11), .pin6(n7408_4_pin5[0]),
    .pin13(OVERWRITE_CHECKER_ON_NEGATED_DATA_pin6), .pin12(A_ARG_4), .pin11(n7408_4_pin5[3]),
    .pin10(OVERWRITE_CHECKER_ON_NEGATED_DATA_pin3), .pin9(A_ARG_5), .pin8(n7408_4_pin5[2]));
  _7408 REGISTER_00_ACCUMULATOR (
    .pin1(ADDER_CHIP_pin5[1]), .pin2(REGISTER_SELECTOR_pin11), .pin3(REGISTER_00_ACCUMULATOR_pin3),
    .pin4(ADDER_CHIP_pin5[0]), .pin5(REGISTER_SELECTOR_pin11), .pin6(REGISTER_00_ACCUMULATOR_pin6),
    .pin13(ADDER_CHIP_pin5[3]), .pin12(REGISTER_SELECTOR_pin11), .pin11(REGISTER_00_ACCUMULATOR_pin11),
    .pin10(ADDER_CHIP_pin5[2]), .pin9(REGISTER_SELECTOR_pin11), .pin8(REGISTER_00_ACCUMULATOR_pin8));
  _7408 REGISTER_01_ACCUMULATOR (
    .pin1(SUBTRACTER_INPUT_NEGATER_pin4[1]), .pin2(REGISTER_SELECTOR_pin8),
    .pin3(REGISTER_01_ACCUMULATOR_pin3), .pin4(SUBTRACTER_INPUT_NEGATER_pin4[0]),
    .pin5(REGISTER_SELECTOR_pin8), .pin6(REGISTER_01_ACCUMULATOR_pin6),
    .pin13(SUBTRACTER_INPUT_NEGATER_pin4[3]), .pin12(REGISTER_SELECTOR_pin8),
    .pin11(REGISTER_01_ACCUMULATOR_pin11), .pin10(SUBTRACTER_INPUT_NEGATER_pin4[2]),
    .pin9(REGISTER_SELECTOR_pin8), .pin8(REGISTER_01_ACCUMULATOR_pin8));
  _7408 REGISTER_10_ACCUMULATOR (
    .pin1(register_3_q[1]), .pin2(REGISTER_SELECTOR_pin3), .pin3(REGISTER_10_ACCUMULATOR_pin3),
    .pin4(register_3_q[0]), .pin5(REGISTER_SELECTOR_pin3), .pin6(REGISTER_10_ACCUMULATOR_pin6),
    .pin13(register_3_q[3]), .pin12(REGISTER_SELECTOR_pin3), .pin11(REGISTER_10_ACCUMULATOR_pin11),
    .pin10(register_3_q[2]), .pin9(REGISTER_SELECTOR_pin3), .pin8(REGISTER_10_ACCUMULATOR_pin8));
  _7408 REGISTER_11_ACCUMULATOR (
    .pin1(register_4_q[1]), .pin2(REGISTER_SELECTOR_pin6), .pin3(REGISTER_11_ACCUMULATOR_pin3),
    .pin4(register_4_q[0]), .pin5(REGISTER_SELECTOR_pin6), .pin6(REGISTER_11_ACCUMULATOR_pin6),
    .pin13(register_4_q[3]), .pin12(REGISTER_SELECTOR_pin6), .pin11(REGISTER_11_ACCUMULATOR_pin11),
    .pin10(register_4_q[2]), .pin9(REGISTER_SELECTOR_pin6), .pin8(REGISTER_11_ACCUMULATOR_pin8));
  _7432 FINAL_OUTPUT_ACCUMULATORS (
    .pin1(ARITHEMETIC_GENERAL_OUTPUT_SIGNAL_CHECKER_pin11), .pin2(O3_ACCUMULATOR_out), .pin3(O3),
    .pin4(ARITHEMETIC_GENERAL_OUTPUT_SIGNAL_CHECKER_pin8), .pin5(O2_ACCUMULATOR_out), .pin6(O2),
    .pin13(O1_ACCUMULATOR_out), .pin12(ARITHEMETIC_GENERAL_OUTPUT_SIGNAL_CHECKER_pin3), .pin11(O1),
    .pin10(O0_ACCUMULATOR_out), .pin9(ARITHEMETIC_GENERAL_OUTPUT_SIGNAL_CHECKER_pin6), .pin8(O0));
  or or_1 (REGISTER_OUT_CHECKERS_pin12, REGISTER_00_ACCUMULATOR_pin11, REGISTER_01_ACCUMULATOR_pin11, REGISTER_10_ACCUMULATOR_pin11, REGISTER_11_ACCUMULATOR_pin11);
  or or_2 (REGISTER_OUT_CHECKERS_pin10, REGISTER_00_ACCUMULATOR_pin8, REGISTER_01_ACCUMULATOR_pin8, REGISTER_10_ACCUMULATOR_pin8, REGISTER_11_ACCUMULATOR_pin8);
  or or_3 (REGISTER_OUT_CHECKERS_pin2, REGISTER_00_ACCUMULATOR_pin3, REGISTER_01_ACCUMULATOR_pin3, REGISTER_10_ACCUMULATOR_pin3, REGISTER_11_ACCUMULATOR_pin3);
  or or_4 (REGISTER_OUT_CHECKERS_pin5, REGISTER_00_ACCUMULATOR_pin6, REGISTER_01_ACCUMULATOR_pin6, REGISTER_10_ACCUMULATOR_pin6, REGISTER_11_ACCUMULATOR_pin6);
  _7408 u_7408_5 (
    .pin1(OPCODE_NEGATERS_pin6), .pin2(O2), .pin3(n7432_2_pin1[1]), .pin4(OPCODE_NEGATERS_pin6), .pin5(O3),
    .pin6(n7432_2_pin1[0]), .pin13(OPCODE_NEGATERS_pin6), .pin12(O0), .pin11(n7432_2_pin1[3]),
    .pin10(OPCODE_NEGATERS_pin6), .pin9(O1), .pin8(n7432_2_pin1[2]));
  // also tied to GND on the sheet: ADDER_CHIP_pin7
  // also tied to VCC on the sheet: SUBTRACTER_CHIP_pin7

  // Notes on the sheet:
  //   1001 - LDA - ADDR
  //   1010 - WRIT - ADDR, REG (2 bit literal)
  //   LDA LOADS TO REGISTER 3 (11)
  //   ALU - 0 is the highest bit
  //   1000 - SAV - ADDR, LITERAL
  //   subtracter unit
  //   adder unit
  //   AND_CHECKERS
  //   SAV_LINE
  //   LDA_LINE
  //   OR_CHECKERS
  //   WRIT_LINE
  //   100 - NOT
  //   101 - XOR
  //   110 - OR
  //   111 - AND
  //   (only on D0)
  //   XOR CHECKERS
  //   NOT CHECKERS
  //   THIS UNIT ENSURES THAT EXTERNAL INPUT GETS PRIORITY
  //   dual 4 input or
  //   Replace these with 2 4072 ICs
  //   REPLACE WITH 4072s
endmodule

module TTL7473 (
  input  J0,
  input  K0,
  input  CLK0,
  input  R0,
  input  J1,
  input  K1,
  input  CLK1,
  input  R1,
  output Q0,
  output P0,
  output Q1,
  output P1
);

  wire undriven, undriven_2;

  J_K_Flip_Flop j_k_ff_1 (.J(J0), .K(K0), .clk(CLK0), .Q(Q0), .Qn(P0), .preset(undriven), .reset(R0));
  J_K_Flip_Flop j_k_ff_2 (.J(J1), .K(K1), .clk(CLK1), .Q(Q1), .Qn(P1), .preset(undriven_2), .reset(R1));
endmodule

module TTL_PC (
  input  [3:0] HIGHLIGHTED_REG,
  input  [3:0] REG_11,
  input  EXEC_MODE,
  input  OP0,
  input  OP1,
  input  OP2,
  input  OP3,
  input  A_ARG_0,
  input  A_ARG_1,
  input  A_ARG_2,
  input  A_ARG_3,
  input  A_ARG_4,
  input  A_ARG_5,
  input  A_ARG_6,
  input  A_ARG_7,
  input  B_ARG_0,
  input  B_ARG_1,
  input  B_ARG_2,
  input  B_ARG_3,
  input  B_ARG_4,
  input  B_ARG_5,
  input  B_ARG_6,
  input  B_ARG_7,
  output O5,
  output O4,
  output out_26,
  output out_27,
  output out_28,
  output out_29,
  output [3:0] out_30,
  output [7:0] out_31,
  output [7:0] out_32
);

  wire n7400_2_pin11, n7408_1_pin1, n7408_1_pin2, n7408_1_pin3, n7408_1_pin4, n7408_1_pin5, n7408_2_pin3,
       n7408_2_pin6, n7408_2_pin8, n7408_5_pin4, n7408_5_pin5, n7421_1_pin4, n7421_1_pin5, n7421_1_pin6,
       n7421_1_pin8, n7421_2_pin1, n7421_2_pin2, n7421_2_pin4, n7421_2_pin5, n7432_1_pin3, n7432_1_pin6,
       n7432_1_pin8, n7432_2_pin1, n7432_2_pin2, n7432_2_pin3, n7432_2_pin8, n7432_2_pin10, n7432_2_pin11,
       n7432_2_pin12, n7432_2_pin13, n7432_3_pin1, n7432_3_pin3, n7432_3_pin4, n7432_3_pin6, n7432_3_pin11,
       n7432_3_pin12, n7432_4_pin2, n7432_4_pin12, RESET_out;

  _7408 u_7408_1 (
    .pin1(n7408_1_pin1), .pin2(n7408_1_pin2), .pin3(n7408_1_pin3), .pin4(n7408_1_pin4), .pin5(n7408_1_pin5));  // open: pin6, pin13, pin12, pin11, pin10, pin9, pin8
  Button RESET (.out(RESET_out));
  Button CLK (.out(n7408_1_pin5));
  _7432 u_7432_1 (
    .pin1(n7408_1_pin5), .pin2(n7408_1_pin5), .pin3(n7432_1_pin3), .pin4(n7432_1_pin3), .pin5(n7408_1_pin3),
    .pin6(n7432_1_pin6), .pin10(RESET_out), .pin9(n7408_1_pin4), .pin8(n7432_1_pin8));  // open: pin13, pin12, pin11
  Button GO (.out(n7408_1_pin1));
  _7432 u_7432_2 (
    .pin1(n7432_2_pin1), .pin2(n7432_2_pin2), .pin3(n7432_2_pin3), .pin13(n7432_2_pin13),
    .pin12(n7432_2_pin12), .pin11(n7432_2_pin11), .pin10(n7432_2_pin10), .pin9(O5), .pin8(n7432_2_pin8));  // open: pin4, pin5, pin6
  _7400 u_7400_1 (
    .pin13(n7432_1_pin8), .pin12(n7432_1_pin8), .pin11(n7432_2_pin13));  // open: pin1, pin2, pin3, pin4, pin5, pin6, pin10, pin9, pin8
  TTL7473 ttl7473_1 (
    .K0(n7432_2_pin11), .J0(n7432_2_pin11), .CLK0(n7432_1_pin6), .R0(n7432_1_pin8), .J1(n7432_2_pin8),
    .K1(n7432_2_pin8), .CLK1(n7432_1_pin6), .R1(n7432_1_pin8), .Q0(O5), .Q1(O4));  // open: P0, P1
  _7408 u_7408_2 (
    .pin1(n7432_2_pin2), .pin2(out_26), .pin3(n7408_2_pin3), .pin4(n7408_2_pin3), .pin5(out_27),
    .pin6(n7408_2_pin6), .pin13(O5), .pin12(O4), .pin11(n7432_2_pin2), .pin10(out_28), .pin9(n7408_2_pin6),
    .pin8(n7408_2_pin8));
  _7432 u_7432_3 (
    .pin1(n7432_3_pin1), .pin2(n7408_2_pin6), .pin3(n7432_3_pin3), .pin4(n7432_3_pin4), .pin5(n7432_3_pin3),
    .pin6(n7432_3_pin6), .pin13(n7408_2_pin3), .pin12(n7432_3_pin12), .pin11(n7432_3_pin11));  // open: pin10, pin9, pin8
  TTL7473 ttl7473_2 (
    .K0(n7432_2_pin3), .J0(n7432_2_pin3), .CLK0(n7432_1_pin6), .R0(n7432_1_pin8), .J1(n7432_3_pin11),
    .K1(n7432_3_pin11), .CLK1(n7432_1_pin6), .R1(n7432_1_pin8), .Q0(out_26), .Q1(out_27));  // open: P0, P1
  TTL7473 ttl7473_3 (
    .K0(n7432_3_pin6), .J0(n7432_3_pin6), .CLK0(n7432_1_pin6), .R0(n7432_1_pin8), .J1(n7408_2_pin8),
    .K1(n7408_2_pin8), .CLK1(n7432_1_pin6), .R1(n7432_1_pin8), .Q0(out_28), .Q1(out_29));  // open: P0, P1
  _7408 u_7408_3 (
    .pin13(n7408_1_pin2), .pin12(out_31[4]), .pin11(n7432_3_pin1), .pin10(n7408_1_pin2), .pin9(out_31[5]),
    .pin8(n7432_3_pin4));  // open: pin1, pin2, pin3, pin4, pin5, pin6
  _7408 u_7408_4 (
    .pin1(n7408_1_pin2), .pin2(out_31[0]), .pin3(n7432_2_pin12), .pin4(n7408_1_pin2), .pin5(out_31[1]),
    .pin6(n7432_2_pin10), .pin13(n7408_1_pin2), .pin12(out_31[3]), .pin11(n7432_3_pin12),
    .pin10(n7408_1_pin2), .pin9(out_31[2]), .pin8(n7432_2_pin1));
  RAM #(.addrWidth(6), .dataWidth(4)) ram_1 (
    .addr({out_29, out_28, out_27, out_26, O4, O5}), .we(n7400_2_pin11), .oe(n7408_1_pin5),
    .clk(n7408_1_pin5), .din({OP0, OP1, OP2, OP3}), .dout(out_30));
  RAM #(.addrWidth(6)) ram_2 (
    .addr({out_29, out_28, out_27, out_26, O4, O5}), .we(n7400_2_pin11), .oe(n7408_1_pin5),
    .clk(n7408_1_pin5), .din({A_ARG_0, A_ARG_1, A_ARG_2, A_ARG_3, A_ARG_4, A_ARG_5, A_ARG_6, A_ARG_7}),
    .dout(out_31));
  RAM #(.addrWidth(6)) ram_3 (
    .addr({out_29, out_28, out_27, out_26, O4, O5}), .we(n7400_2_pin11), .oe(n7408_1_pin5),
    .clk(n7408_1_pin5), .din({B_ARG_0, B_ARG_1, B_ARG_2, B_ARG_3, B_ARG_4, B_ARG_5, B_ARG_6, B_ARG_7}),
    .dout(out_32));
  _7421 u_7421_1 (
    .pin1(out_30[3]), .pin2(out_30[2]), .pin4(n7421_1_pin4), .pin5(n7421_1_pin5), .pin6(n7421_1_pin6),
    .pin13(n7421_1_pin6), .pin12(n7421_1_pin6), .pin10(n7408_1_pin5), .pin9(n7408_1_pin5), .pin8(n7421_1_pin8));  // open: pin3, pin11
  _7432 u_7432_4 (
    .pin1(n7421_1_pin8), .pin2(n7432_4_pin2), .pin3(n7408_1_pin4), .pin13(n7421_1_pin6),
    .pin12(n7432_4_pin12), .pin11(n7408_1_pin2));  // open: pin4, pin5, pin6, pin10, pin9, pin8
  _7400 u_7400_2 (
    .pin1(out_30[1]), .pin2(out_30[1]), .pin3(n7421_1_pin4), .pin4(out_30[0]), .pin5(out_30[0]),
    .pin6(n7421_1_pin5), .pin13(EXEC_MODE), .pin12(EXEC_MODE), .pin11(n7400_2_pin11));  // open: pin10, pin9, pin8
  _7408 u_7408_5 (
    .pin4(n7408_5_pin4), .pin5(n7408_5_pin5), .pin6(n7432_4_pin12), .pin10(n7408_1_pin5),
    .pin9(n7432_4_pin12), .pin8(n7432_4_pin2));  // open: pin1, pin2, pin3, pin13, pin12, pin11
  _7421 u_7421_2 (
    .pin1(n7421_2_pin1), .pin2(n7421_2_pin2), .pin4(n7421_2_pin4), .pin5(n7421_2_pin5), .pin6(n7408_5_pin5),
    .pin13(out_30[0]), .pin12(n7421_1_pin4), .pin10(out_30[2]), .pin9(out_30[3]), .pin8(n7408_5_pin4));  // open: pin3, pin11
  xnor xnor_1 (n7421_2_pin5, HIGHLIGHTED_REG[0], REG_11[0]);
  xnor xnor_2 (n7421_2_pin4, HIGHLIGHTED_REG[1], REG_11[1]);
  xnor xnor_3 (n7421_2_pin2, HIGHLIGHTED_REG[2], REG_11[2]);
  xnor xnor_4 (n7421_2_pin1, HIGHLIGHTED_REG[3], REG_11[3]);

  // Notes on the sheet:
  //   RESET
  //   TWO HIGHEST BITS IGNORED
  //   EQUIVALENT
  //   repalce with 747266
endmodule
