// Logisim project 4bitcomp.circ as structural Verilog
module RAM_1_Nibble (
  input  D0,
  input  CLK,
  input  D1,
  input  D2,
  input  D3,
  output O0,
  output O1,
  output O2,
  output O3
);

  D_Flip_Flop d_ff_1 (.D(D0), .clk(CLK), .Q(O0));  // open: Qn, preset, reset
  D_Flip_Flop d_ff_2 (.D(D1), .clk(CLK), .Q(O1));  // open: Qn, preset, reset
  D_Flip_Flop d_ff_3 (.D(D2), .clk(CLK), .Q(O2));  // open: Qn, preset, reset
  D_Flip_Flop d_ff_4 (.D(D3), .clk(CLK), .Q(O3));  // open: Qn, preset, reset
endmodule

module RAM_4_Nibble (
  input  A0,
  input  A1,
  input  CLK,
  input  D0,
  input  D1,
  input  D2,
  input  D3,
  output O0,
  output O1,
  output O2,
  output O3
);

  wire and_1_out, and_2_out, and_3_out, and_4_out, and_5_out, and_6_out, and_7_out, and_8_out, and_9_out,
       and_10_out, and_11_out, and_12_out, and_13_out, and_14_out, and_15_out, and_16_out, and_17_out,
       and_18_out, and_19_out, and_20_out, DATA_00_o0, DATA_00_o1, DATA_00_o2, DATA_00_o3, DATA_01_o0,
       DATA_01_o1, DATA_01_o2, DATA_01_o3, DATA_10_o0, DATA_10_o1, DATA_10_o2, DATA_10_o3, DATA_11_o0,
       DATA_11_o1, DATA_11_o2, DATA_11_o3, not_1_out, not_2_out, SCENARIO_00_out, SCENARIO_01_out,
       SCENARIO_10_out, SCENARIO_11_out;

  not not_1 (not_1_out, A0);
  not not_2 (not_2_out, A1);
  and SCENARIO_11 (SCENARIO_11_out, A0, A1);
  and SCENARIO_10 (SCENARIO_10_out, A0, not_2_out);
  and SCENARIO_01 (SCENARIO_01_out, not_1_out, A1);
  and SCENARIO_00 (SCENARIO_00_out, not_1_out, not_2_out);
  and and_1 (and_1_out, SCENARIO_11_out, CLK);
  and and_2 (and_2_out, SCENARIO_10_out, CLK);
  and and_3 (and_3_out, SCENARIO_01_out, CLK);
  and and_4 (and_4_out, SCENARIO_00_out, CLK);
  and and_5 (and_5_out, DATA_11_o0, SCENARIO_11_out);
  and and_6 (and_6_out, DATA_11_o1, SCENARIO_11_out);
  RAM_1_Nibble DATA_11 (
    .D0(D0), .CLK(and_1_out), .D1(D1), .D2(D2), .D3(D3), .O0(DATA_11_o0), .O1(DATA_11_o1), .O2(DATA_11_o2),
    .O3(DATA_11_o3));
  and and_7 (and_7_out, DATA_11_o2, SCENARIO_11_out);
  and and_8 (and_8_out, DATA_11_o3, SCENARIO_11_out);
  and and_9 (and_9_out, DATA_10_o0, SCENARIO_10_out);
  and and_10 (and_10_out, DATA_10_o1, SCENARIO_10_out);
  RAM_1_Nibble DATA_10 (
    .D0(D0), .CLK(and_2_out), .D1(D1), .D2(D2), .D3(D3), .O0(DATA_10_o0), .O1(DATA_10_o1), .O2(DATA_10_o2),
    .O3(DATA_10_o3));
  and and_11 (and_11_out, DATA_10_o2, SCENARIO_10_out);
  and and_12 (and_12_out, DATA_10_o3, SCENARIO_10_out);
  and and_13 (and_13_out, DATA_01_o0, SCENARIO_01_out);
  and and_14 (and_14_out, DATA_01_o1, SCENARIO_01_out);
  RAM_1_Nibble DATA_01 (
    .D0(D0), .CLK(and_3_out), .D1(D1), .D2(D2), .D3(D3), .O0(DATA_01_o0), .O1(DATA_01_o1), .O2(DATA_01_o2),
    .O3(DATA_01_o3));
  and and_15 (and_15_out, DATA_01_o2, SCENARIO_01_out);
  and and_16 (and_16_out, DATA_01_o3, SCENARIO_01_out);
  and and_17 (and_17_out, DATA_00_o0, SCENARIO_00_out);
  and and_18 (and_18_out, DATA_00_o1, SCENARIO_00_out);
  RAM_1_Nibble DATA_00 (
    .D0(D0), .CLK(and_4_out), .D1(D1), .D2(D2), .D3(D3), .O0(DATA_00_o0), .O1(DATA_00_o1), .O2(DATA_00_o2),
    .O3(DATA_00_o3));
  and and_19 (and_19_out, DATA_00_o2, SCENARIO_00_out);
  and and_20 (and_20_out, DATA_00_o3, SCENARIO_00_out);
  or O2_ACCUMULATOR (O2, and_11_out, and_7_out, and_15_out, and_19_out);
  or O3_ACCUMULATOR (O3, and_8_out, and_12_out, and_16_out, and_20_out);
  or O0_ACCUMULATOR (O0, and_5_out, and_9_out, and_13_out, and_17_out);
  or O1_ACCUMULATOR (O1, and_6_out, and_10_out, and_14_out, and_18_out);
endmodule

module RAM_16_Nibble (
  input  D0,
  input  D1,
  input  D2,
  input  D3,
  input  A0,
  input  A1,
  input  CLK,
  input  A2,
  input  A3,
  output O0,
  output O1,
  output O2,
  output O3
);

  wire and_1_out, and_2_out, and_3_out, and_4_out, and_5_out, and_6_out, and_7_out, and_8_out, and_9_out,
       and_10_out, and_11_out, and_12_out, and_13_out, and_14_out, and_15_out, and_16_out, and_17_out,
       and_18_out, and_19_out, and_20_out, DATA_00_o0, DATA_00_o1, DATA_00_o2, DATA_00_o3, DATA_01_o0,
       DATA_01_o1, DATA_01_o2, DATA_01_o3, DATA_10_o0, DATA_10_o1, DATA_10_o2, DATA_10_o3, DATA_11_o0,
       DATA_11_o1, DATA_11_o2, DATA_11_o3, not_1_out, not_2_out, SCENARIO_00_out, SCENARIO_01_out,
       SCENARIO_10_out, SCENARIO_11_out;

  not not_1 (not_1_out, A2);
  not not_2 (not_2_out, A3);
  and SCENARIO_11 (SCENARIO_11_out, A2, A3);
  and SCENARIO_10 (SCENARIO_10_out, A2, not_2_out);
  and SCENARIO_01 (SCENARIO_01_out, not_1_out, A3);
  and SCENARIO_00 (SCENARIO_00_out, not_1_out, not_2_out);
  and and_1 (and_1_out, CLK, SCENARIO_11_out);
  and and_2 (and_2_out, CLK, SCENARIO_10_out);
  and and_3 (and_3_out, CLK, SCENARIO_01_out);
  and and_4 (and_4_out, CLK, SCENARIO_00_out);
  RAM_4_Nibble DATA_11 (
    .A0(A0), .A1(A1), .CLK(and_1_out), .D0(D0), .D1(D1), .D2(D2), .D3(D3), .O0(DATA_11_o0), .O1(DATA_11_o1),
    .O2(DATA_11_o2), .O3(DATA_11_o3));
  RAM_4_Nibble DATA_10 (
    .A0(A0), .A1(A1), .CLK(and_2_out), .D0(D0), .D1(D1), .D2(D2), .D3(D3), .O0(DATA_10_o0), .O1(DATA_10_o1),
    .O2(DATA_10_o2), .O3(DATA_10_o3));
  RAM_4_Nibble DATA_01 (
    .A0(A0), .A1(A1), .CLK(and_3_out), .D0(D0), .D1(D1), .D2(D2), .D3(D3), .O0(DATA_01_o0), .O1(DATA_01_o1),
    .O2(DATA_01_o2), .O3(DATA_01_o3));
  RAM_4_Nibble DATA_00 (
    .A0(A0), .A1(A1), .CLK(and_4_out), .D0(D0), .D1(D1), .D2(D2), .D3(D3), .O0(DATA_00_o0), .O1(DATA_00_o1),
    .O2(DATA_00_o2), .O3(DATA_00_o3));
  and and_5 (and_5_out, DATA_11_o0, SCENARIO_11_out);
  and and_6 (and_6_out, DATA_11_o1, SCENARIO_11_out);
  and and_7 (and_7_out, DATA_11_o2, SCENARIO_11_out);
  and and_8 (and_8_out, DATA_11_o3, SCENARIO_11_out);
  and and_9 (and_9_out, DATA_10_o0, SCENARIO_10_out);
  and and_10 (and_10_out, DATA_10_o1, SCENARIO_10_out);
  and and_11 (and_11_out, DATA_10_o2, SCENARIO_10_out);
  and and_12 (and_12_out, DATA_10_o3, SCENARIO_10_out);
  and and_13 (and_13_out, DATA_01_o0, SCENARIO_01_out);
  and and_14 (and_14_out, DATA_01_o1, SCENARIO_01_out);
  and and_15 (and_15_out, DATA_01_o2, SCENARIO_01_out);
  and and_16 (and_16_out, DATA_01_o3, SCENARIO_01_out);
  and and_17 (and_17_out, DATA_00_o0, SCENARIO_00_out);
  and and_18 (and_18_out, DATA_00_o1, SCENARIO_00_out);
  and and_19 (and_19_out, DATA_00_o2, SCENARIO_00_out);
  and and_20 (and_20_out, DATA_00_o3, SCENARIO_00_out);
  or O0_ACCUMULATOR (O0, and_5_out, and_9_out, and_13_out, and_17_out);
  or O1_ACCUMULATOR (O1, and_6_out, and_10_out, and_14_out, and_18_out);
  or O2_ACCUMULATOR (O2, and_7_out, and_11_out, and_15_out, and_19_out);
  or O3_ACCUMULATOR (O3, and_8_out, and_12_out, and_16_out, and_20_out);
endmodule

module RAM_64_Nibble (
  input  D0,
  input  D1,
  input  D2,
  input  D3,
  input  A0,
  input  A1,
  input  A2,
  input  A3,
  input  CLK,
  input  A4,
  input  A5,
  output O0,
  output O1,
  output O2,
  output O3
);

  wire and_1_out, and_2_out, and_3_out, and_4_out, and_5_out, and_6_out, and_7_out, and_8_out, and_9_out,
       and_10_out, and_11_out, and_12_out, and_13_out, and_14_out, and_15_out, and_16_out, and_17_out,
       and_18_out, and_19_out, and_20_out, DATA_01_o0, DATA_01_o1, DATA_01_o2, DATA_01_o3, DATA_10_o0,
       DATA_10_o1, DATA_10_o2, DATA_10_o3, DATA_11_o0, DATA_11_o1, DATA_11_o2, DATA_11_o3, not_1_out,
       not_2_out, ram_16_nibble_1_o0, ram_16_nibble_1_o1, ram_16_nibble_1_o2, ram_16_nibble_1_o3,
       SCENARIO_00_out, SCENARIO_01_out, SCENARIO_10_out, SCENARIO_11_out;

  not not_1 (not_1_out, A4);
  not not_2 (not_2_out, A5);
  and SCENARIO_11 (SCENARIO_11_out, A4, A5);
  and SCENARIO_10 (SCENARIO_10_out, A4, not_2_out);
  and SCENARIO_01 (SCENARIO_01_out, not_1_out, A5);
  and SCENARIO_00 (SCENARIO_00_out, not_1_out, not_2_out);
  and and_1 (and_1_out, CLK, SCENARIO_11_out);
  and and_2 (and_2_out, CLK, SCENARIO_10_out);
  and and_3 (and_3_out, CLK, SCENARIO_01_out);
  and and_4 (and_4_out, CLK, SCENARIO_00_out);
  RAM_16_Nibble DATA_11 (
    .D0(D0), .D1(D1), .D2(D2), .D3(D3), .A0(A0), .A1(A1), .CLK(and_1_out), .A2(A2), .A3(A3), .O0(DATA_11_o0),
    .O1(DATA_11_o1), .O2(DATA_11_o2), .O3(DATA_11_o3));
  RAM_16_Nibble DATA_10 (
    .D0(D0), .D1(D1), .D2(D2), .D3(D3), .A0(A0), .A1(A1), .CLK(and_2_out), .A2(A2), .A3(A3), .O0(DATA_10_o0),
    .O1(DATA_10_o1), .O2(DATA_10_o2), .O3(DATA_10_o3));
  and and_5 (and_5_out, DATA_11_o0, CLK);
  and and_6 (and_6_out, DATA_11_o1, CLK);
  and and_7 (and_7_out, DATA_11_o2, CLK);
  and and_8 (and_8_out, DATA_11_o3, CLK);
  and and_9 (and_9_out, DATA_10_o0, SCENARIO_10_out);
  and and_10 (and_10_out, DATA_10_o1, SCENARIO_10_out);
  and and_11 (and_11_out, DATA_10_o2, SCENARIO_10_out);
  and and_12 (and_12_out, DATA_10_o3, SCENARIO_10_out);
  and and_13 (and_13_out, DATA_01_o0, SCENARIO_01_out);
  and and_14 (and_14_out, DATA_01_o1, SCENARIO_01_out);
  RAM_16_Nibble DATA_01 (
    .D0(D0), .D1(D1), .D2(D2), .D3(D3), .A0(A0), .A1(A1), .CLK(and_3_out), .A2(A2), .A3(A3), .O0(DATA_01_o0),
    .O1(DATA_01_o1), .O2(DATA_01_o2), .O3(DATA_01_o3));
  and and_15 (and_15_out, DATA_01_o2, SCENARIO_01_out);
  and and_16 (and_16_out, DATA_01_o3, SCENARIO_01_out);
  and and_17 (and_17_out, ram_16_nibble_1_o0, SCENARIO_00_out);
  and and_18 (and_18_out, ram_16_nibble_1_o1, SCENARIO_00_out);
  RAM_16_Nibble ram_16_nibble_1 (
    .D0(D0), .D1(D1), .D2(D2), .D3(D3), .A0(A0), .A1(A1), .CLK(and_4_out), .A2(A2), .A3(A3),
    .O0(ram_16_nibble_1_o0), .O1(ram_16_nibble_1_o1), .O2(ram_16_nibble_1_o2), .O3(ram_16_nibble_1_o3));
  and and_19 (and_19_out, ram_16_nibble_1_o2, SCENARIO_00_out);
  and and_20 (and_20_out, ram_16_nibble_1_o3, SCENARIO_00_out);
  or O0_ACCUMULATOR (O0, and_5_out, and_9_out, and_13_out, and_17_out);
  or O1_ACCUMULATOR (O1, and_6_out, and_10_out, and_14_out, and_18_out);
  or O2_ACCUMULATOR (O2, and_7_out, and_11_out, and_15_out, and_19_out);
  or O3_ACCUMULATOR (O3, and_8_out, and_12_out, and_16_out, and_20_out);
endmodule

module RAM_256_Nibble (
  input  D0,
  input  D1,
  input  D2,
  input  D3,
  input  A0,
  input  A1,
  input  A2,
  input  A3,
  input  A4,
  input  A5,
  input  CLK,
  input  A6,
  input  A7,
  output O0,
  output O1,
  output O2,
  output O3
);

  wire and_1_out, and_2_out, and_3_out, and_4_out, and_5_out, and_6_out, and_7_out, and_8_out, and_9_out,
       and_10_out, and_11_out, and_12_out, and_13_out, and_14_out, and_15_out, and_16_out, and_17_out,
       and_18_out, and_19_out, and_20_out, DATA_00_o0, DATA_00_o1, DATA_00_o2, DATA_00_o3, DATA_01_o0,
       DATA_01_o1, DATA_01_o2, DATA_01_o3, DATA_10_o0, DATA_10_o1, DATA_10_o2, DATA_10_o3, DATA_11_o0,
       DATA_11_o1, DATA_11_o2, DATA_11_o3, not_1_out, not_2_out, SCENARIO_00_out, SCENARIO_01_out,
       SCENARIO_10_out, SCENARIO_11_out;

  not not_1 (not_1_out, A6);
  not not_2 (not_2_out, A7);
  and SCENARIO_11 (SCENARIO_11_out, A6, A7);
  and SCENARIO_10 (SCENARIO_10_out, A6, not_2_out);
  and SCENARIO_01 (SCENARIO_01_out, not_1_out, A7);
  and SCENARIO_00 (SCENARIO_00_out, not_1_out, not_2_out);
  and and_1 (and_1_out, CLK, SCENARIO_11_out);
  and and_2 (and_2_out, CLK, SCENARIO_10_out);
  and and_3 (and_3_out, CLK, SCENARIO_01_out);
  and and_4 (and_4_out, CLK, SCENARIO_00_out);
  and and_5 (and_5_out, DATA_11_o0, SCENARIO_11_out);
  and and_6 (and_6_out, DATA_11_o1, SCENARIO_11_out);
  RAM_64_Nibble DATA_11 (
    .D0(D0), .D1(D1), .D2(D2), .D3(D3), .A0(A0), .A1(A1), .A2(A2), .A3(A3), .CLK(and_1_out), .A4(A4),
    .A5(A5), .O0(DATA_11_o0), .O1(DATA_11_o1), .O2(DATA_11_o2), .O3(DATA_11_o3));
  and and_7 (and_7_out, DATA_11_o2, SCENARIO_11_out);
  and and_8 (and_8_out, DATA_11_o3, SCENARIO_11_out);
  and and_9 (and_9_out, DATA_10_o0, SCENARIO_10_out);
  and and_10 (and_10_out, DATA_10_o1, SCENARIO_10_out);
  RAM_64_Nibble DATA_10 (
    .D0(D0), .D1(D1), .D2(D2), .D3(D3), .A0(A0), .A1(A1), .A2(A2), .A3(A3), .CLK(and_2_out), .A4(A4),
    .A5(A5), .O0(DATA_10_o0), .O1(DATA_10_o1), .O2(DATA_10_o2), .O3(DATA_10_o3));
  and and_11 (and_11_out, DATA_10_o2, SCENARIO_10_out);
  and and_12 (and_12_out, DATA_10_o3, SCENARIO_10_out);
  and and_13 (and_13_out, DATA_01_o0, SCENARIO_01_out);
  and and_14 (and_14_out, DATA_01_o1, SCENARIO_01_out);
  RAM_64_Nibble DATA_01 (
    .D0(D0), .D1(D1), .D2(D2), .D3(D3), .A0(A0), .A1(A1), .A2(A2), .A3(A3), .CLK(and_3_out), .A4(A4),
    .A5(A5), .O0(DATA_01_o0), .O1(DATA_01_o1), .O2(DATA_01_o2), .O3(DATA_01_o3));
  and and_15 (and_15_out, DATA_01_o2, SCENARIO_01_out);
  and and_16 (and_16_out, DATA_01_o3, SCENARIO_01_out);
  and and_17 (and_17_out, DATA_00_o0, SCENARIO_00_out);
  and and_18 (and_18_out, DATA_00_o1, SCENARIO_00_out);
  RAM_64_Nibble DATA_00 (
    .D0(D0), .D1(D1), .D2(D2), .D3(D3), .A0(A0), .A1(A1), .A2(A2), .A3(A3), .CLK(and_4_out), .A4(A4),
    .A5(A5), .O0(DATA_00_o0), .O1(DATA_00_o1), .O2(DATA_00_o2), .O3(DATA_00_o3));
  and and_19 (and_19_out, DATA_00_o2, SCENARIO_00_out);
  and and_20 (and_20_out, DATA_00_o3, SCENARIO_00_out);
  or O0_ACCUMULATOR (O0, and_5_out, and_9_out, and_13_out, and_17_out);
  or O1_ACCUMULATOR (O1, and_6_out, and_10_out, and_14_out, and_18_out);
  or O3_ACCUMULATOR (O3, and_8_out, and_12_out, and_16_out, and_20_out);
  or O2_ACCUMULATOR (O2, and_7_out, and_11_out, and_15_out, and_19_out);
endmodule

module ALU (
  input  OP0,
  input  OP1,
  input  OP2,
  input  D0,
  input  E0,
  input  D1,
  input  E1,
  input  D2,
  input  E2,
  input  D3,
  input  E3,
  output O0,
  output O1,
  output O2,
  output O3,
  output ERROR_BIT
);

  wire and_1_out, and_2_out, and_3_out, and_4_out, and_5_out, and_6_out, and_7_out, and_8_out, and_9_out,
       arithmetic_1_error_bit, arithmetic_1_out0, arithmetic_1_out1, arithmetic_1_out2, arithmetic_1_out3,
       logic_4_bit_1_o0, logic_4_bit_1_o1, logic_4_bit_1_o2, logic_4_bit_1_o3, not_1_out, not_2_out;

  not not_1 (not_1_out, OP0);
  and and_1 (and_1_out, not_1_out, OP2);
  and and_2 (and_2_out, logic_4_bit_1_o0, OP0);
  and and_3 (and_3_out, logic_4_bit_1_o1, OP0);
  LOGIC_4_BIT logic_4_bit_1 (
    .OP0(OP0), .OP1(OP1), .OP2(OP2), .D0(D0), .E0(E0), .D1(D1), .E1(E1), .D2(D2), .E2(E2), .D3(D3), .E3(E3),
    .O0(logic_4_bit_1_o0), .O1(logic_4_bit_1_o1), .O2(logic_4_bit_1_o2), .O3(logic_4_bit_1_o3));
  and and_4 (and_4_out, logic_4_bit_1_o2, OP0);
  and and_5 (and_5_out, logic_4_bit_1_o3, OP0);
  and and_6 (and_6_out, arithmetic_1_out3, not_2_out);
  and and_7 (and_7_out, arithmetic_1_out2, not_2_out);
  ARITHMETIC arithmetic_1 (
    .D3(D3), .E3(E3), .D2(D2), .E2(E2), .D1(D1), .E1(E1), .D0(D0), .E0(E0), .SUBTRACTION_BIT(and_1_out),
    .OUT3(arithmetic_1_out3), .OUT2(arithmetic_1_out2), .OUT1(arithmetic_1_out1), .OUT0(arithmetic_1_out0),
    .ERROR_BIT(arithmetic_1_error_bit));
  and and_8 (and_8_out, arithmetic_1_out1, not_2_out);
  and and_9 (and_9_out, arithmetic_1_out0, not_2_out);
  and and_10 (ERROR_BIT, arithmetic_1_error_bit, not_2_out);
  not not_2 (not_2_out, OP0);
  or O0_ACCUMULATOR (O0, and_2_out, and_9_out);
  or O1_ACCUMULATOR (O1, and_3_out, and_8_out);
  or O2_ACCUMULATOR (O2, and_4_out, and_7_out);
  or O3_ACCUMULATOR (O3, and_5_out, and_6_out);

  // Notes on the sheet:
  //   ALU - 0 is the highest bit
  //   000 - ADD
  //   001 - SUB
  //   010 - NOP
  //   011 - NOP
  //   100 - NOT
  //   101 - XOR
  //   110 - OR
  //   111 - AND
  //   (only on D3)
endmodule

module LOGIC (
  input  OP0,
  input  OP1,
  input  OP2,
  input  D0,
  input  E0,
  output O
);

  wire and_1_out, and_2_out, and_3_out, and_4_out, and_5_out, and_6_out, and_7_out, and_8_out, and_9_out,
       AND_CHECKER_out, not_1_out, not_2_out, not_3_out, NOT_CHECKER_out, or_1_out, OR_CHECKER_out,
       xor_1_out, XOR_CHECKER_out;

  not not_1 (not_1_out, OP1);
  not not_2 (not_2_out, OP2);
  and and_1 (and_1_out, OP1, OP2);
  and and_2 (and_2_out, OP1, not_2_out);
  and and_3 (and_3_out, not_1_out, OP2);
  and and_4 (and_4_out, not_1_out, not_2_out);
  and and_5 (and_5_out, OP0, and_1_out);
  and and_6 (and_6_out, OP0, and_2_out);
  and and_7 (and_7_out, OP0, and_3_out);
  and and_8 (and_8_out, OP0, and_4_out);
  and and_9 (and_9_out, D0, E0);
  or or_1 (or_1_out, D0, E0);
  xor xor_1 (xor_1_out, D0, E0);
  not not_3 (not_3_out, D0);
  and AND_CHECKER (AND_CHECKER_out, and_5_out, and_9_out);
  and OR_CHECKER (OR_CHECKER_out, and_6_out, or_1_out);
  and XOR_CHECKER (XOR_CHECKER_out, and_7_out, xor_1_out);
  and NOT_CHECKER (NOT_CHECKER_out, and_8_out, not_3_out);
  or or_2 (O, AND_CHECKER_out, OR_CHECKER_out, XOR_CHECKER_out, NOT_CHECKER_out);

  // Notes on the sheet:
  //   100 - NOT
  //   101 - XOR
  //   110 - OR
  //   111 - AND
  //   All prefixed by 1 - designed to be interfaced with the arithmetic unit (prefixed by 0)
  //   Logic Unit
  //   Takes data on D0 and E0
  //   (only on D0)
endmodule

module ARITHMETIC (
  input  D3,
  input  E3,
  input  D2,
  input  E2,
  input  D1,
  input  E1,
  input  D0,
  input  E0,
  input  SUBTRACTION_BIT,
  output OUT3,
  output OUT2,
  output OUT1,
  output OUT0,
  output ERROR_BIT
);

  wire adder_4_bit_carry_1_carry_out, adder_4_bit_carry_1_sum0, adder_4_bit_carry_1_sum1,
       adder_4_bit_carry_1_sum2, adder_4_bit_carry_1_sum3, and_1_out, and_2_out, and_3_out, and_4_out,
       and_5_out, and_6_out, and_7_out, and_8_out, and_9_out, and_10_out, not_1_out,
       subtracter_4_bit_overflow_1_diff0, subtracter_4_bit_overflow_1_diff1,
       subtracter_4_bit_overflow_1_diff2, subtracter_4_bit_overflow_1_diff3,
       subtracter_4_bit_overflow_1_overflow;

  and and_1 (and_1_out, adder_4_bit_carry_1_sum3, not_1_out);
  and and_2 (and_2_out, adder_4_bit_carry_1_sum2, not_1_out);
  Adder_4_Bit_Carry adder_4_bit_carry_1 (
    .D3(D3), .E3(E3), .D2(D2), .E2(E2), .D1(D1), .E1(E1), .D0(D0), .E0(E0), .SUM3(adder_4_bit_carry_1_sum3),
    .SUM2(adder_4_bit_carry_1_sum2), .SUM1(adder_4_bit_carry_1_sum1), .SUM0(adder_4_bit_carry_1_sum0),
    .CARRY_OUT(adder_4_bit_carry_1_carry_out));
  and and_3 (and_3_out, adder_4_bit_carry_1_sum1, not_1_out);
  and and_4 (and_4_out, adder_4_bit_carry_1_sum0, not_1_out);
  and and_5 (and_5_out, adder_4_bit_carry_1_carry_out, not_1_out);
  and and_6 (and_6_out, subtracter_4_bit_overflow_1_diff3, SUBTRACTION_BIT);
  and and_7 (and_7_out, subtracter_4_bit_overflow_1_diff2, SUBTRACTION_BIT);
  Subtracter_4_Bit_Overflow subtracter_4_bit_overflow_1 (
    .D3(D3), .E3(E3), .D2(D2), .E2(E2), .D1(D1), .E1(E1), .D0(D0), .E0(E0),
    .DIFF3(subtracter_4_bit_overflow_1_diff3), .DIFF2(subtracter_4_bit_overflow_1_diff2),
    .DIFF1(subtracter_4_bit_overflow_1_diff1), .DIFF0(subtracter_4_bit_overflow_1_diff0),
    .OVERFLOW(subtracter_4_bit_overflow_1_overflow));
  and and_8 (and_8_out, subtracter_4_bit_overflow_1_diff1, SUBTRACTION_BIT);
  and and_9 (and_9_out, subtracter_4_bit_overflow_1_diff0, SUBTRACTION_BIT);
  and and_10 (and_10_out, subtracter_4_bit_overflow_1_overflow, SUBTRACTION_BIT);
  not not_1 (not_1_out, SUBTRACTION_BIT);
  or or_1 (OUT3, and_1_out, and_6_out);
  or or_2 (OUT2, and_2_out, and_7_out);
  or or_3 (OUT1, and_3_out, and_8_out);
  or or_4 (OUT0, and_4_out, and_9_out);
  or or_5 (ERROR_BIT, and_5_out, and_10_out);
endmodule

module Adder_1_Bit_With_Carry (
  input  CARRY_IN,
  input  D0,
  input  D1,
  output SUM,
  output CARRY_OUT
);

  wire and_1_out, and_2_out, and_3_out, nand_1_out, nand_2_out, or_1_out, or_2_out;

  or or_1 (or_1_out, D0, D1);
  nand nand_1 (nand_1_out, D0, D1);
  and and_1 (and_1_out, D0, D1);
  and and_2 (and_2_out, or_1_out, nand_1_out);
  or or_2 (or_2_out, CARRY_IN, and_2_out);
  nand nand_2 (nand_2_out, CARRY_IN, and_2_out);
  and and_3 (and_3_out, CARRY_IN, and_2_out);
  and and_4 (SUM, or_2_out, nand_2_out);
  or or_3 (CARRY_OUT, and_3_out, and_1_out);
endmodule

module Adder_4_Bit_Carry (
  input  D3,
  input  E3,
  input  D2,
  input  E2,
  input  D1,
  input  E1,
  input  D0,
  input  E0,
  output SUM3,
  output SUM2,
  output SUM1,
  output SUM0,
  output CARRY_OUT
);

  wire ADD_1_carry_out, ADD_2_carry_out, ADD_3_carry_out;

  Adder_1_Bit_With_Carry ADD_3 (.CARRY_IN(1'b0), .D0(D3), .D1(E3), .SUM(SUM3), .CARRY_OUT(ADD_3_carry_out));
  Adder_1_Bit_With_Carry ADD_2 (.CARRY_IN(ADD_3_carry_out), .D0(D2), .D1(E2), .SUM(SUM2), .CARRY_OUT(ADD_2_carry_out));
  Adder_1_Bit_With_Carry ADD_1 (.CARRY_IN(ADD_2_carry_out), .D0(D1), .D1(E1), .SUM(SUM1), .CARRY_OUT(ADD_1_carry_out));
  Adder_1_Bit_With_Carry ADD_0 (.CARRY_IN(ADD_1_carry_out), .D0(D0), .D1(E0), .SUM(SUM0), .CARRY_OUT(CARRY_OUT));

  // Notes on the sheet:
  //   0 is the highest bit
endmodule

module Subtracter_4_Bit_Overflow (
  input  D3,
  input  E3,
  input  D2,
  input  E2,
  input  D1,
  input  E1,
  input  D0,
  input  E0,
  output DIFF3,
  output DIFF2,
  output DIFF1,
  output DIFF0,
  output OVERFLOW
);

  wire not_1_out, not_2_out, not_3_out, not_4_out, SUB_0_carry_out, SUB_1_carry_out, SUB_2_carry_out,
       SUB_3_carry_out;

  not not_1 (not_1_out, E3);
  not not_2 (not_2_out, E2);
  not not_3 (not_3_out, E1);
  not not_4 (not_4_out, E0);
  Adder_1_Bit_With_Carry SUB_3 (.CARRY_IN(1'b1), .D0(D3), .D1(not_1_out), .SUM(DIFF3), .CARRY_OUT(SUB_3_carry_out));
  Adder_1_Bit_With_Carry SUB_2 (
    .CARRY_IN(SUB_3_carry_out), .D0(D2), .D1(not_2_out), .SUM(DIFF2), .CARRY_OUT(SUB_2_carry_out));
  Adder_1_Bit_With_Carry SUB_1 (
    .CARRY_IN(SUB_2_carry_out), .D0(D1), .D1(not_3_out), .SUM(DIFF1), .CARRY_OUT(SUB_1_carry_out));
  Adder_1_Bit_With_Carry SUB_0 (
    .CARRY_IN(SUB_1_carry_out), .D0(D0), .D1(not_4_out), .SUM(DIFF0), .CARRY_OUT(SUB_0_carry_out));
  not not_5 (OVERFLOW, SUB_0_carry_out);

  // Notes on the sheet:
  //   0 is the highest bit
endmodule

module LOGIC_4_BIT (
  input  OP0,
  input  OP1,
  input  OP2,
  input  D0,
  input  E0,
  input  D1,
  input  E1,
  input  D2,
  input  E2,
  input  D3,
  input  E3,
  output O0,
  output O1,
  output O2,
  output O3
);

  wire and_1_out, and_2_out, and_3_out, and_4_out, and_5_out, and_6_out, and_7_out, and_8_out, and_9_out,
       and_10_out, and_11_out, and_12_out, and_13_out, and_14_out, and_15_out, and_16_out, and_17_out,
       and_18_out, and_19_out, and_20_out, and_21_out, and_22_out, and_23_out, and_24_out, and_25_out,
       and_26_out, and_27_out, and_28_out, not_1_out, not_2_out, not_3_out, not_4_out, not_5_out, not_6_out,
       or_1_out, or_2_out, or_3_out, or_4_out, xor_1_out, xor_2_out, xor_3_out, xor_4_out;

  not not_1 (not_1_out, OP1);
  not not_2 (not_2_out, OP2);
  and and_1 (and_1_out, OP1, OP2);
  and and_2 (and_2_out, OP1, not_2_out);
  and and_3 (and_3_out, not_1_out, OP2);
  and and_4 (and_4_out, not_1_out, not_2_out);
  and and_5 (and_5_out, OP0, and_1_out);
  and and_6 (and_6_out, OP0, and_2_out);
  and and_7 (and_7_out, OP0, and_3_out);
  and and_8 (and_8_out, OP0, and_4_out);
  and and_9 (and_9_out, D0, E0);
  and and_10 (and_10_out, D1, E1);
  and and_11 (and_11_out, D2, E2);
  and and_12 (and_12_out, D3, E3);
  and and_13 (and_13_out, and_9_out, and_5_out);
  and and_14 (and_14_out, and_10_out, and_5_out);
  and and_15 (and_15_out, and_11_out, and_5_out);
  and and_16 (and_16_out, and_12_out, and_5_out);
  or or_1 (or_1_out, D0, E0);
  or or_2 (or_2_out, D1, E1);
  or or_3 (or_3_out, D2, E2);
  or or_4 (or_4_out, D3, E3);
  and and_17 (and_17_out, or_1_out, and_6_out);
  and and_18 (and_18_out, or_2_out, and_6_out);
  and and_19 (and_19_out, or_3_out, and_6_out);
  and and_20 (and_20_out, or_4_out, and_6_out);
  xor xor_1 (xor_1_out, D0, E0);
  xor xor_2 (xor_2_out, D1, E1);
  xor xor_3 (xor_3_out, D2, E2);
  xor xor_4 (xor_4_out, D3, E3);
  not not_3 (not_3_out, D0);
  not not_4 (not_4_out, D1);
  not not_5 (not_5_out, D2);
  not not_6 (not_6_out, D3);
  and and_21 (and_21_out, xor_1_out, and_7_out);
  and and_22 (and_22_out, xor_2_out, and_7_out);
  and and_23 (and_23_out, xor_3_out, and_7_out);
  and and_24 (and_24_out, xor_4_out, and_7_out);
  and and_25 (and_25_out, and_8_out, not_3_out);
  and and_26 (and_26_out, and_8_out, not_4_out);
  and and_27 (and_27_out, and_8_out, not_5_out);
  and and_28 (and_28_out, and_8_out, not_6_out);
  or O0_ACCUMULATOR (O0, and_25_out, and_21_out, and_17_out, and_13_out);
  or O1_ACCUMULATOR (O1, and_26_out, and_22_out, and_18_out, and_14_out);
  or O2_ACCUMULATOR (O2, and_27_out, and_23_out, and_19_out, and_15_out);
  or O3_ACCUMULATOR (O3, and_28_out, and_24_out, and_20_out, and_16_out);

  // Notes on the sheet:
  //   AND_CHECKERS
  //   OR_CHECKERS
  //   100 - NOT
  //   101 - XOR
  //   110 - OR
  //   111 - AND
  //   XOR CHECKERS
  //   (only on D0)
  //   NOT CHECKERS
endmodule

module CONTROL (
  input  GO,
  input  OP0,
  input  OP1,
  input  OP2,
  input  OP3,
  input  A_ARG_0,
  input  A_ARG_1,
  input  A_ARG_2,
  input  A_ARG_3,
  input  A_ARG_4,
  input  A_ARG_5,
  input  A_ARG_6,
  input  A_ARG_7,
  input  B_ARG_0,
  input  B_ARG_1,
  input  B_ARD_2,
  input  B_ARG_3,
  input  B_ARG_4,
  input  B_ARG_5,
  input  B_ARG_6,
  input  B_ARG_7,
  output O0,
  output O1,
  output O2,
  output O3,
  output ERROR_BIT
);

  wire alu_1_error_bit, alu_1_o0, alu_1_o1, alu_1_o2, alu_1_o3, and_1_out, and_2_out, and_3_out, and_4_out,
       and_5_out, and_6_out, and_7_out, and_9_out, and_10_out, and_11_out, and_12_out, and_13_out,
       and_14_out, and_15_out, and_16_out, and_17_out, memory_1_o0, memory_1_o1, memory_1_o2, memory_1_o3,
       not_1_out;

  not not_1 (not_1_out, OP0);
  and and_1 (and_1_out, OP1, not_1_out);
  and and_2 (and_2_out, OP2, not_1_out);
  and and_3 (and_3_out, OP3, not_1_out);
  and and_4 (and_4_out, GO, and_9_out);
  and and_5 (and_5_out, GO, and_10_out);
  and and_6 (and_6_out, GO, and_11_out);
  and and_7 (and_7_out, GO, and_12_out);
  and and_8 (ERROR_BIT, GO, and_13_out);
  and and_9 (and_9_out, alu_1_o0, not_1_out);
  and and_10 (and_10_out, alu_1_o1, not_1_out);
  ALU alu_1 (
    .OP0(and_1_out), .OP1(and_2_out), .OP2(and_3_out), .D0(A_ARG_4), .E0(B_ARG_4), .D1(A_ARG_5),
    .E1(B_ARG_5), .D2(A_ARG_6), .E2(B_ARG_6), .D3(A_ARG_7), .E3(B_ARG_7), .O0(alu_1_o0), .O1(alu_1_o1),
    .O2(alu_1_o2), .O3(alu_1_o3), .ERROR_BIT(alu_1_error_bit));
  and and_11 (and_11_out, alu_1_o2, not_1_out);
  and and_12 (and_12_out, alu_1_o3, not_1_out);
  and and_13 (and_13_out, alu_1_error_bit, not_1_out);
  and and_14 (and_14_out, memory_1_o0, OP0);
  and and_15 (and_15_out, memory_1_o1, OP0);
  MEMORY memory_1 (
    .OP0(OP0), .OP1(OP1), .OP2(OP2), .OP3(OP3), .A_ARG_0(A_ARG_0), .A_ARG_1(A_ARG_1), .A_ARG_2(A_ARG_2),
    .A_ARG_3(A_ARG_3), .A_ARG_4(A_ARG_4), .A_ARG_5(A_ARG_5), .A_ARG_6(A_ARG_6), .A_ARG_7(A_ARG_7),
    .B_ARG_0(B_ARG_0), .B_ARG_1(B_ARG_1), .B_ARD_2(B_ARD_2), .B_ARG_3(B_ARG_3), .B_ARG_4(B_ARG_4),
    .B_ARG_5(B_ARG_5), .B_ARG_6(B_ARG_6), .B_ARG_7(B_ARG_7), .GO(GO), .O0(memory_1_o0), .O1(memory_1_o1),
    .O2(memory_1_o2), .O3(memory_1_o3));
  and and_16 (and_16_out, memory_1_o2, OP0);
  and and_17 (and_17_out, memory_1_o3, OP0);
  or or_1 (O0, and_4_out, and_14_out);
  or or_2 (O1, and_5_out, and_15_out);
  or or_3 (O2, and_6_out, and_16_out);
  or or_4 (O3, and_7_out, and_17_out);
  LED led_1 (.in(O0));
  LED led_2 (.in(O1));
  LED led_3 (.in(O2));
  LED led_4 (.in(O3));
  LED led_5 (.in(ERROR_BIT));

  // Notes on the sheet:
  //   000 - ADD - LITERAL, LITERAL
  //   001 - SUB - LITERAL, LITERAL
  //   010 - NOP - IGNORED x2
  //   011 - NOP - IGNORED x2
  //   100 - NOT - LITERAL, IGNORED
  //   101 - XOR - LITERAL, LITERAL
  //   110 - OR - LITERAL, LITERAL
  //   111 - AND - LITERAL, LITERAL
  //   1000 - SAV - LITERAL, ADDR
  //   1001 - MOV - ADDR, ADDR
  //   This is the control unit - it takes in an opcode and two input sets
  //   OP0 through 3 are op codes - specified above
  //   The A_ARG and B_ARG sets are either a binary literal or a memory address
  //   This depends on the opcode, again specified above
  //   If they are literals, the top 4 bits must be 0 - the bottom 4 are the relevant ones
endmodule

module MEMORY (
  input  OP0,
  input  OP1,
  input  OP2,
  input  OP3,
  input  A_ARG_0,
  input  A_ARG_1,
  input  A_ARG_2,
  input  A_ARG_3,
  input  A_ARG_4,
  input  A_ARG_5,
  input  A_ARG_6,
  input  A_ARG_7,
  input  B_ARG_0,
  input  B_ARG_1,
  input  B_ARD_2,
  input  B_ARG_3,
  input  B_ARG_4,
  input  B_ARG_5,
  input  B_ARG_6,
  input  B_ARG_7,
  input  GO,
  output O0,
  output O1,
  output O2,
  output O3
);

  wire and_1_out, and_2_out, and_3_out, and_4_out, and_5_out, and_6_out, and_7_out, and_8_out, and_9_out,
       and_10_out, and_11_out, and_12_out, and_13_out, and_14_out, and_15_out, and_16_out, and_17_out,
       and_18_out, and_19_out, and_20_out, and_21_out, and_22_out, and_23_out, and_24_out, and_25_out,
       and_26_out, and_27_out, and_28_out, not_1_out, not_2_out, not_3_out, or_1_out, or_2_out, or_3_out,
       or_4_out, or_5_out, or_6_out, or_7_out, or_8_out, or_9_out, or_10_out, or_11_out, or_12_out,
       or_13_out, or_14_out, or_15_out, or_16_out, or_17_out, or_18_out, or_19_out, or_20_out, or_21_out,
       ram_1_nibble_1_o0, ram_1_nibble_1_o1, ram_1_nibble_1_o2, ram_1_nibble_1_o3;

  not not_1 (not_1_out, OP1);
  not not_2 (not_2_out, OP2);
  not not_3 (not_3_out, OP3);
  and and_1 (and_1_out, A_ARG_0, and_22_out);
  and and_2 (and_2_out, A_ARG_1, and_22_out);
  and and_3 (and_3_out, A_ARG_2, and_22_out);
  and and_4 (and_4_out, A_ARG_3, and_22_out);
  or or_1 (or_1_out, and_22_out, and_5_out);
  or or_2 (or_2_out, and_22_out, and_5_out);
  or or_3 (or_3_out, and_22_out, and_5_out);
  or or_4 (or_4_out, and_22_out, and_5_out);
  or or_5 (or_5_out, and_22_out, and_5_out);
  or or_6 (or_6_out, and_22_out, and_5_out);
  or or_7 (or_7_out, and_22_out, and_5_out);
  or or_8 (or_8_out, and_22_out, and_5_out);
  and and_5 (and_5_out, OP0, not_1_out, not_2_out, not_3_out);
  and and_6 (and_6_out, A_ARG_4, and_5_out);
  and and_7 (and_7_out, A_ARG_4, and_22_out);
  and and_8 (and_8_out, A_ARG_5, and_5_out);
  and and_9 (and_9_out, A_ARG_5, and_22_out);
  and and_10 (and_10_out, A_ARG_6, and_5_out);
  and and_11 (and_11_out, A_ARG_6, and_22_out);
  and and_12 (and_12_out, A_ARG_7, and_5_out);
  and and_13 (and_13_out, A_ARG_7, and_22_out);
  and and_14 (and_14_out, B_ARG_0, or_1_out);
  and and_15 (and_15_out, B_ARG_1, or_2_out);
  and and_16 (and_16_out, B_ARD_2, or_3_out);
  and and_17 (and_17_out, B_ARG_3, or_4_out);
  and and_18 (and_18_out, B_ARG_4, or_5_out);
  and and_19 (and_19_out, B_ARG_5, or_6_out);
  and and_20 (and_20_out, B_ARG_6, or_7_out);
  and and_21 (and_21_out, B_ARG_7, or_8_out);
  and and_22 (and_22_out, OP0, not_1_out, not_2_out, OP3);
  or or_9 (or_9_out, and_22_out, and_5_out);
  or or_10 (or_10_out, and_9_out, and_19_out);
  or or_11 (or_11_out, and_11_out, and_20_out);
  or or_12 (or_12_out, and_24_out, and_6_out);
  or or_13 (or_13_out, and_25_out, and_8_out);
  or or_14 (or_14_out, and_26_out, and_10_out);
  or or_15 (or_15_out, and_27_out, and_12_out);
  or or_16 (or_16_out, and_1_out, and_14_out);
  or or_17 (or_17_out, and_2_out, and_15_out);
  or or_18 (or_18_out, and_3_out, and_16_out);
  or or_19 (or_19_out, and_7_out, and_18_out);
  or or_20 (or_20_out, and_4_out, and_17_out);
  and and_23 (and_23_out, or_9_out, GO);
  or or_21 (or_21_out, and_13_out, and_21_out);
  and and_24 (and_24_out, ram_1_nibble_1_o0, and_28_out);
  and and_25 (and_25_out, ram_1_nibble_1_o1, and_28_out);
  and and_26 (and_26_out, ram_1_nibble_1_o2, and_28_out);
  and and_27 (and_27_out, ram_1_nibble_1_o3, and_28_out);
  LED led_1 (.in(O0));
  RAM_256_Nibble ram_256_nibble_1 (
    .D0(or_12_out), .D1(or_13_out), .D2(or_14_out), .D3(or_15_out), .A0(or_16_out), .A1(or_17_out),
    .A2(or_18_out), .A3(or_20_out), .A4(or_19_out), .A5(or_10_out), .CLK(and_23_out), .A6(or_11_out),
    .A7(or_21_out), .O0(O0), .O1(O1), .O2(O2), .O3(O3));
  LED led_2 (.in(O1));
  LED led_3 (.in(O2));
  LED led_4 (.in(O3));
  and and_28 (and_28_out, and_22_out, GO);
  RAM_1_Nibble ram_1_nibble_1 (
    .D0(O0), .CLK(and_22_out), .D1(O1), .D2(O2), .D3(O3), .O0(ram_1_nibble_1_o0), .O1(ram_1_nibble_1_o1),
    .O2(ram_1_nibble_1_o2), .O3(ram_1_nibble_1_o3));

  // Notes on the sheet:
  //   1000 - SAV - LITERAL, ADDR
  //   1001 - MOV - ADDR, ADDR
endmodule

module COUNTER_8_Bit (
  input  CLK,
  input  RESET,
  input  HI,
  output O7,
  output O6,
  output O5,
  output O4,
  output O3,
  output O2,
  output O1,
  output O0
);

  wire and_1_out, and_2_out, and_3_out, and_4_out, and_5_out, or_1_out, or_2_out, or_3_out, or_4_out,
       or_5_out, or_6_out, or_7_out, or_8_out;

  J_K_Flip_Flop j_k_ff_1 (.J(1'b1), .K(1'b1), .clk(or_1_out), .Q(O7), .reset(RESET));  // open: Qn, preset
  or or_1 (or_1_out, CLK, HI);
  or or_2 (or_2_out, HI, O7);
  J_K_Flip_Flop j_k_ff_2 (.J(or_2_out), .K(or_2_out), .clk(or_1_out), .Q(O6), .reset(RESET));  // open: Qn, preset
  and and_1 (and_1_out, O7, O6);
  J_K_Flip_Flop j_k_ff_3 (.J(or_3_out), .K(or_3_out), .clk(or_1_out), .Q(O5), .reset(RESET));  // open: Qn, preset
  or or_3 (or_3_out, HI, and_1_out);
  and and_2 (and_2_out, O5, and_1_out);
  J_K_Flip_Flop j_k_ff_4 (.J(or_4_out), .K(or_4_out), .clk(or_1_out), .Q(O4), .reset(RESET));  // open: Qn, preset
  or or_4 (or_4_out, HI, and_2_out);
  J_K_Flip_Flop j_k_ff_5 (.J(or_5_out), .K(or_5_out), .clk(or_1_out), .Q(O3), .reset(RESET));  // open: Qn, preset
  or or_5 (or_5_out, HI, and_3_out);
  and and_3 (and_3_out, O4, and_2_out);
  J_K_Flip_Flop j_k_ff_6 (.J(or_6_out), .K(or_6_out), .clk(or_1_out), .Q(O2), .reset(RESET));  // open: Qn, preset
  or or_6 (or_6_out, HI, and_4_out);
  and and_4 (and_4_out, and_3_out, O3);
  and and_5 (and_5_out, O2, and_4_out);
  J_K_Flip_Flop j_k_ff_7 (.J(or_7_out), .K(or_7_out), .clk(or_1_out), .Q(O1), .reset(RESET));  // open: Qn, preset
  or or_7 (or_7_out, HI, and_5_out);
  J_K_Flip_Flop j_k_ff_8 (.J(or_8_out), .K(or_8_out), .clk(or_1_out), .Q(O0), .reset(RESET));  // open: Qn, preset
  or or_8 (or_8_out, HI, O0);
  // AND_Gate and_6 has open pins: in0=and_5_out, in1=O1, out=open
endmodule

module PROGRAM_COUNTER (
  input  OP0,
  input  OP1,
  input  OP2,
  input  OP3,
  input  A_ARG_0,
  input  A_ARG_1,
  input  A_ARG_2,
  input  A_ARG_3,
  input  A_ARG_4,
  input  A_ARG_5,
  input  A_ARG_6,
  input  A_ARG_7,
  input  B_ARG_0,
  input  B_ARG_1,
  input  B_ARD_2,
  input  B_ARG_3,
  input  B_ARG_4,
  input  B_ARG_5,
  input  B_ARG_6,
  input  B_ARG_7
);

  wire clock_1_out, counter_8_bit_1_o2, counter_8_bit_1_o3, counter_8_bit_1_o4, counter_8_bit_1_o5,
       counter_8_bit_1_o6, counter_8_bit_1_o7, CPU_error_bit, CPU_o0, CPU_o1, CPU_o2, CPU_o3, GO_out,
       or_1_out, ram_64_nibble_1_o0, ram_64_nibble_1_o1, ram_64_nibble_1_o2, ram_64_nibble_1_o3,
       ram_64_nibble_2_o0, ram_64_nibble_2_o1, ram_64_nibble_2_o2, ram_64_nibble_2_o3, ram_64_nibble_3_o0,
       ram_64_nibble_3_o1, ram_64_nibble_3_o2, ram_64_nibble_3_o3, ram_64_nibble_4_o0, ram_64_nibble_4_o1,
       ram_64_nibble_4_o2, ram_64_nibble_4_o3, ram_64_nibble_5_o0, ram_64_nibble_5_o1, ram_64_nibble_5_o2,
       ram_64_nibble_5_o3, START_EXECUTION_out;

  Button START_EXECUTION (.out(START_EXECUTION_out));
  or or_1 (or_1_out, clock_1_out, GO_out);
  Clock clock_1 (.out(clock_1_out));
  COUNTER_8_Bit counter_8_bit_1 (
    .CLK(or_1_out), .HI(START_EXECUTION_out), .O7(counter_8_bit_1_o7), .O6(counter_8_bit_1_o6),
    .O5(counter_8_bit_1_o5), .O4(counter_8_bit_1_o4), .O3(counter_8_bit_1_o3), .O2(counter_8_bit_1_o2));  // open: RESET, O1, O0
  Button GO (.out(GO_out));
  RAM_64_Nibble ram_64_nibble_1 (
    .D0(OP0), .D1(OP1), .D2(OP2), .D3(OP3), .A0(counter_8_bit_1_o2), .A1(counter_8_bit_1_o3),
    .A2(counter_8_bit_1_o4), .A3(counter_8_bit_1_o5), .CLK(GO_out), .A4(counter_8_bit_1_o6),
    .A5(counter_8_bit_1_o7), .O0(ram_64_nibble_1_o0), .O1(ram_64_nibble_1_o1), .O2(ram_64_nibble_1_o2),
    .O3(ram_64_nibble_1_o3));
  RAM_64_Nibble ram_64_nibble_2 (
    .D0(A_ARG_0), .D1(A_ARG_1), .D2(A_ARG_2), .D3(A_ARG_3), .A0(counter_8_bit_1_o2), .A1(counter_8_bit_1_o3),
    .A2(counter_8_bit_1_o4), .A3(counter_8_bit_1_o5), .CLK(GO_out), .A4(counter_8_bit_1_o6),
    .A5(counter_8_bit_1_o7), .O0(ram_64_nibble_2_o0), .O1(ram_64_nibble_2_o1), .O2(ram_64_nibble_2_o2),
    .O3(ram_64_nibble_2_o3));
  RAM_64_Nibble ram_64_nibble_3 (
    .D0(A_ARG_4), .D1(A_ARG_5), .D2(A_ARG_6), .D3(A_ARG_7), .A0(counter_8_bit_1_o2), .A1(counter_8_bit_1_o3),
    .A2(counter_8_bit_1_o4), .A3(counter_8_bit_1_o5), .CLK(GO_out), .A4(counter_8_bit_1_o6),
    .A5(counter_8_bit_1_o7), .O0(ram_64_nibble_3_o0), .O1(ram_64_nibble_3_o1), .O2(ram_64_nibble_3_o2),
    .O3(ram_64_nibble_3_o3));
  RAM_64_Nibble ram_64_nibble_4 (
    .D0(B_ARG_0), .D1(B_ARG_1), .D2(B_ARD_2), .D3(B_ARG_3), .A0(counter_8_bit_1_o2), .A1(counter_8_bit_1_o3),
    .A2(counter_8_bit_1_o4), .A3(counter_8_bit_1_o5), .CLK(GO_out), .A4(counter_8_bit_1_o6),
    .A5(counter_8_bit_1_o7), .O0(ram_64_nibble_4_o0), .O1(ram_64_nibble_4_o1), .O2(ram_64_nibble_4_o2),
    .O3(ram_64_nibble_4_o3));
  RAM_64_Nibble ram_64_nibble_5 (
    .D0(B_ARG_4), .D1(B_ARG_5), .D2(B_ARG_6), .D3(B_ARG_7), .A0(counter_8_bit_1_o2), .A1(counter_8_bit_1_o3),
    .A2(counter_8_bit_1_o4), .A3(counter_8_bit_1_o5), .CLK(GO_out), .A4(counter_8_bit_1_o6),
    .A5(counter_8_bit_1_o7), .O0(ram_64_nibble_5_o0), .O1(ram_64_nibble_5_o1), .O2(ram_64_nibble_5_o2),
    .O3(ram_64_nibble_5_o3));
  LED led_1 (.in(CPU_o0));
  CONTROL CPU (
    .GO(clock_1_out), .OP0(ram_64_nibble_1_o0), .OP1(ram_64_nibble_1_o1), .OP2(ram_64_nibble_1_o2),
    .OP3(ram_64_nibble_1_o3), .A_ARG_0(ram_64_nibble_2_o0), .A_ARG_1(ram_64_nibble_2_o1),
    .A_ARG_2(ram_64_nibble_2_o2), .A_ARG_3(ram_64_nibble_2_o3), .A_ARG_4(ram_64_nibble_3_o0),
    .A_ARG_5(ram_64_nibble_3_o1), .A_ARG_6(ram_64_nibble_3_o2), .A_ARG_7(ram_64_nibble_3_o3),
    .B_ARG_0(ram_64_nibble_4_o0), .B_ARG_1(ram_64_nibble_4_o1), .B_ARD_2(ram_64_nibble_4_o2),
    .B_ARG_3(ram_64_nibble_4_o3), .B_ARG_4(ram_64_nibble_5_o0), .B_ARG_5(ram_64_nibble_5_o1),
    .B_ARG_6(ram_64_nibble_5_o2), .B_ARG_7(ram_64_nibble_5_o3), .O0(CPU_o0), .O1(CPU_o1), .O2(CPU_o2),
    .O3(CPU_o3), .ERROR_BIT(CPU_error_bit));
  LED led_2 (.in(CPU_o1));
  LED led_3 (.in(CPU_o2));
  LED led_4 (.in(CPU_o3));
  LED led_5 (.in(CPU_error_bit));

  // Notes on the sheet:
  //   001 - SUB - LITERAL, LITERAL
  //   010 - NOP - IGNORED x2
  //   011 - NOP - IGNORED x2
  //   101 - XOR - LITERAL, LITERAL
  //   110 - OR - LITERAL, LITERAL
  //   1000 - SAV - LITERAL, ADDR
  //   1001 - MOV - ADDR, ADDR
  //   000 - ADD - LITERAL, LITERAL
  //   100 - NOT - LITERAL, IGNORED
  //   111 - AND - LITERAL, LITERAL
  //   The inputs are for programming mode - the op is written  to the next address.
endmodule
